// Logisim project CPU_MEM_1.circ as structural Verilog
module CPU_MEM_1 (
  input  s,
  input  e,
  output e_2
);

  wire nand_1_out, nand_2_out, nand_4_out;

  nand nand_1 (nand_1_out, s, e);
  nand nand_2 (nand_2_out, nand_1_out, e);
  nand nand_3 (e_2, nand_1_out, nand_4_out);
  nand nand_4 (nand_4_out, e_2, nand_2_out);
endmodule
