// Logisim project DESIGN_CPU.circ as structural Verilog: 11 circuits, main circuit main
module main (
  input  [7:0] in_1,
  input  in_2,
  input  in_3,
  output [7:0] out_4
);

  CPU_REG_8 cpu_reg_8_1 (.in_1(in_1), .out_4(out_4), .in_2(in_3), .in_3(in_2));
endmodule

module CPU_MEM_8 (
  input  [7:0] i,
  input  s,
  output [7:0] o
);

  CPU_MEM_1 cpu_mem_1_1 (.s(i[0]), .e(s), .e_2(o[0]));
  CPU_MEM_1 cpu_mem_1_2 (.s(i[1]), .e(s), .e_2(o[1]));
  CPU_MEM_1 cpu_mem_1_3 (.s(i[2]), .e(s), .e_2(o[2]));
  CPU_MEM_1 cpu_mem_1_4 (.s(i[3]), .e(s), .e_2(o[3]));
  CPU_MEM_1 cpu_mem_1_5 (.s(i[4]), .e(s), .e_2(o[4]));
  CPU_MEM_1 cpu_mem_1_6 (.s(i[5]), .e(s), .e_2(o[5]));
  CPU_MEM_1 cpu_mem_1_7 (.s(i[6]), .e(s), .e_2(o[6]));
  CPU_MEM_1 cpu_mem_1_8 (.s(i[7]), .e(s), .e_2(o[7]));
endmodule

module CPU_ENABLE (
  input  [7:0] in_1,
  input  in_2,
  output [7:0] out_3
);

  and and_1 (out_3[0], in_1[0], in_2);
  and and_2 (out_3[1], in_1[1], in_2);
  and and_3 (out_3[2], in_1[2], in_2);
  and and_4 (out_3[3], in_1[3], in_2);
  and and_5 (out_3[4], in_1[4], in_2);
  and and_6 (out_3[5], in_1[5], in_2);
  and and_7 (out_3[6], in_1[6], in_2);
  and and_8 (out_3[7], in_1[7], in_2);
endmodule

module CPU_REG_8 (
  input  [7:0] in_1,
  input  in_2,
  input  in_3,
  output [7:0] out_4
);

  wire [7:0] cpu_mem_8_1_o;

  CPU_MEM_8 cpu_mem_8_1 (.i(in_1), .s(in_2), .o(cpu_mem_8_1_o));
  CPU_ENABLE cpu_enable_1 (.out_3(out_4), .in_1(cpu_mem_8_1_o), .in_2(in_3));
endmodule

module CPU_DECODER_2X4 (
  input  in_1,
  input  in_2,
  output out_3,
  output out_4,
  output out_5,
  output out_6
);

  wire not_1_out, not_2_out;

  not not_1 (not_1_out, in_1);
  not not_2 (not_2_out, in_2);
  and and_1 (out_3, not_1_out, not_2_out);
  and and_2 (out_4, not_1_out, in_2);
  and and_3 (out_5, in_1, not_2_out);
  and and_4 (out_6, in_1, in_2);
endmodule

module CPU_DECODER_4X16 (
  input  [3:0] \input ,
  input  enable,
  output [15:0] out_3
);

  wire cpu_decoder_2x4e_1_out_4, cpu_decoder_2x4e_1_out_5, cpu_decoder_2x4e_1_out_6, cpu_decoder_2x4e_1_out_7;

  CPU_DECODER_2X4E cpu_decoder_2x4e_1 (
    .in_3(1'b1), .out_4(cpu_decoder_2x4e_1_out_4), .out_5(cpu_decoder_2x4e_1_out_5),
    .out_6(cpu_decoder_2x4e_1_out_6), .out_7(cpu_decoder_2x4e_1_out_7), .in_1(\input [2]), .in_2(\input [3]));
  CPU_DECODER_2X4E cpu_decoder_2x4e_2 (
    .in_3(cpu_decoder_2x4e_1_out_4), .out_4(out_3[0]), .out_5(out_3[1]), .out_6(out_3[2]), .out_7(out_3[3]),
    .in_1(\input [0]), .in_2(\input [1]));
  CPU_DECODER_2X4E cpu_decoder_2x4e_3 (
    .in_3(cpu_decoder_2x4e_1_out_5), .out_4(out_3[4]), .out_5(out_3[5]), .out_6(out_3[6]), .out_7(out_3[7]),
    .in_1(\input [0]), .in_2(\input [1]));
  CPU_DECODER_2X4E cpu_decoder_2x4e_4 (
    .in_3(cpu_decoder_2x4e_1_out_6), .out_4(out_3[8]), .out_5(out_3[9]), .out_6(out_3[10]),
    .out_7(out_3[11]), .in_1(\input [0]), .in_2(\input [1]));
  CPU_DECODER_2X4E cpu_decoder_2x4e_5 (
    .in_3(cpu_decoder_2x4e_1_out_7), .out_4(out_3[12]), .out_5(out_3[13]), .out_6(out_3[14]),
    .out_7(out_3[15]), .in_1(\input [0]), .in_2(\input [1]));
endmodule

module CPU_DECODER_2X4E (
  input  in_1,
  input  in_2,
  input  in_3,
  output out_4,
  output out_5,
  output out_6,
  output out_7
);

  wire not_1_out, not_2_out;

  not not_1 (not_1_out, in_1);
  not not_2 (not_2_out, in_2);
  and and_1 (out_4, in_3, not_1_out, not_2_out);
  and and_2 (out_5, in_3, not_1_out, in_2);
  and and_3 (out_6, in_3, in_1, not_2_out);
  and and_4 (out_7, in_1, in_3, in_2);
endmodule

module CPU_REG_BYTE (
  input  [7:0] in_1,
  input  reset,
  input  h,
  input  v,
  input  s,
  input  e,
  output [7:0] \output 
);

  wire and_1_out, and_2_out, and_3_out, or_1_out;
  wire [7:0] cpu_reg_8_1_out_4;

  and and_1 (and_1_out, h, v);
  and and_2 (and_2_out, and_1_out, s);
  and and_3 (and_3_out, and_1_out, e);
  or or_1 (or_1_out, reset, and_2_out);
  CPU_REG_8 cpu_reg_8_1 (.in_1(in_1), .out_4(cpu_reg_8_1_out_4), .in_2(or_1_out), .in_3(and_3_out));
  CPU_BUFFER_8 cpu_buffer_8_1 (.\input (cpu_reg_8_1_out_4), .enable(and_3_out), .\output (\output ));
endmodule

module CPU_BUFFER_8 (
  input  [7:0] \input ,
  input  enable,
  output [7:0] \output 
);

  and and_1 (\output [0], \input [0], enable);
  and and_2 (\output [1], \input [1], enable);
  and and_3 (\output [2], \input [2], enable);
  and and_4 (\output [3], \input [3], enable);
  and and_5 (\output [4], \input [4], enable);
  and and_6 (\output [5], \input [5], enable);
  and and_7 (\output [6], \input [6], enable);
  and and_8 (\output [7], \input [7], enable);
endmodule

module CPU_RAM_256 (
  input  [7:0] address,
  input  [7:0] \input ,
  input  reset,
  input  set,
  input  enable,
  output [7:0] out_6,
  output [7:0] out_7,
  output [7:0] out_8,
  output [7:0] out_9,
  output [7:0] out_10,
  output [7:0] out_11,
  output [7:0] out_12,
  output [7:0] out_13,
  output [7:0] out_14,
  output [7:0] out_15,
  output [7:0] out_16,
  output [7:0] out_17,
  output [7:0] out_18,
  output [7:0] out_19,
  output [7:0] out_20,
  output [7:0] out_21,
  output [7:0] out_22,
  output [7:0] out_23,
  output [7:0] out_24,
  output [7:0] out_25,
  output [7:0] out_26,
  output [7:0] out_27,
  output [7:0] out_28,
  output [7:0] out_29,
  output [7:0] out_30,
  output [7:0] out_31,
  output [7:0] out_32,
  output [7:0] out_33,
  output [7:0] out_34,
  output [7:0] out_35,
  output [7:0] out_36,
  output [7:0] out_37,
  output [7:0] out_38,
  output [7:0] out_39,
  output [7:0] out_40,
  output [7:0] out_41,
  output [7:0] out_42,
  output [7:0] out_43,
  output [7:0] out_44,
  output [7:0] out_45,
  output [7:0] out_46,
  output [7:0] out_47,
  output [7:0] out_48,
  output [7:0] out_49,
  output [7:0] out_50,
  output [7:0] out_51,
  output [7:0] out_52,
  output [7:0] out_53,
  output [7:0] out_54,
  output [7:0] out_55,
  output [7:0] out_56,
  output [7:0] out_57,
  output [7:0] out_58,
  output [7:0] out_59,
  output [7:0] out_60,
  output [7:0] out_61,
  output [7:0] out_62,
  output [7:0] out_63,
  output [7:0] out_64,
  output [7:0] out_65,
  output [7:0] out_66,
  output [7:0] out_67,
  output [7:0] out_68,
  output [7:0] out_69,
  output [7:0] out_70,
  output [7:0] out_71,
  output [7:0] out_72,
  output [7:0] out_73,
  output [7:0] out_74,
  output [7:0] out_75,
  output [7:0] out_76,
  output [7:0] out_77,
  output [7:0] out_78,
  output [7:0] out_79,
  output [7:0] out_80,
  output [7:0] out_81,
  output [7:0] out_82,
  output [7:0] out_83,
  output [7:0] out_84,
  output [7:0] out_85,
  output [7:0] out_86,
  output [7:0] out_87,
  output [7:0] out_88,
  output [7:0] out_89,
  output [7:0] out_90,
  output [7:0] out_91,
  output [7:0] out_92,
  output [7:0] out_93,
  output [7:0] out_94,
  output [7:0] out_95,
  output [7:0] out_96,
  output [7:0] out_97,
  output [7:0] out_98,
  output [7:0] out_99,
  output [7:0] out_100,
  output [7:0] out_101,
  output [7:0] out_102,
  output [7:0] out_103,
  output [7:0] out_104,
  output [7:0] out_105,
  output [7:0] out_106,
  output [7:0] out_107,
  output [7:0] out_108,
  output [7:0] out_109,
  output [7:0] out_110,
  output [7:0] out_111,
  output [7:0] out_112,
  output [7:0] out_113,
  output [7:0] out_114,
  output [7:0] out_115,
  output [7:0] out_116,
  output [7:0] out_117,
  output [7:0] out_118,
  output [7:0] out_119,
  output [7:0] out_120,
  output [7:0] out_121,
  output [7:0] out_122,
  output [7:0] out_123,
  output [7:0] out_124,
  output [7:0] out_125,
  output [7:0] out_126,
  output [7:0] out_127,
  output [7:0] out_128,
  output [7:0] out_129,
  output [7:0] out_130,
  output [7:0] out_131,
  output [7:0] out_132,
  output [7:0] out_133,
  output [7:0] out_134,
  output [7:0] out_135,
  output [7:0] out_136,
  output [7:0] out_137,
  output [7:0] out_138,
  output [7:0] out_139,
  output [7:0] out_140,
  output [7:0] out_141,
  output [7:0] out_142,
  output [7:0] out_143,
  output [7:0] out_144,
  output [7:0] out_145,
  output [7:0] out_146,
  output [7:0] out_147,
  output [7:0] out_148,
  output [7:0] out_149,
  output [7:0] out_150,
  output [7:0] out_151,
  output [7:0] out_152,
  output [7:0] out_153,
  output [7:0] out_154,
  output [7:0] out_155,
  output [7:0] out_156,
  output [7:0] out_157,
  output [7:0] out_158,
  output [7:0] out_159,
  output [7:0] out_160,
  output [7:0] out_161,
  output [7:0] out_162,
  output [7:0] out_163,
  output [7:0] out_164,
  output [7:0] out_165,
  output [7:0] out_166,
  output [7:0] out_167,
  output [7:0] out_168,
  output [7:0] out_169,
  output [7:0] out_170,
  output [7:0] out_171,
  output [7:0] out_172,
  output [7:0] out_173,
  output [7:0] out_174,
  output [7:0] out_175,
  output [7:0] out_176,
  output [7:0] out_177,
  output [7:0] out_178,
  output [7:0] out_179,
  output [7:0] out_180,
  output [7:0] out_181,
  output [7:0] out_182,
  output [7:0] out_183,
  output [7:0] out_184,
  output [7:0] out_185,
  output [7:0] out_186,
  output [7:0] out_187,
  output [7:0] out_188,
  output [7:0] out_189,
  output [7:0] out_190,
  output [7:0] out_191,
  output [7:0] out_192,
  output [7:0] out_193,
  output [7:0] out_194,
  output [7:0] out_195,
  output [7:0] out_196,
  output [7:0] out_197,
  output [7:0] out_198,
  output [7:0] out_199,
  output [7:0] out_200,
  output [7:0] out_201,
  output [7:0] out_202,
  output [7:0] out_203,
  output [7:0] out_204,
  output [7:0] out_205,
  output [7:0] out_206,
  output [7:0] out_207,
  output [7:0] out_208,
  output [7:0] out_209,
  output [7:0] out_210,
  output [7:0] out_211,
  output [7:0] out_212,
  output [7:0] out_213,
  output [7:0] out_214,
  output [7:0] out_215,
  output [7:0] out_216,
  output [7:0] out_217,
  output [7:0] out_218,
  output [7:0] out_219,
  output [7:0] out_220,
  output [7:0] out_221,
  output [7:0] out_222,
  output [7:0] out_223,
  output [7:0] out_224,
  output [7:0] out_225,
  output [7:0] out_226,
  output [7:0] out_227,
  output [7:0] out_228,
  output [7:0] out_229,
  output [7:0] out_230,
  output [7:0] out_231,
  output [7:0] out_232,
  output [7:0] out_233,
  output [7:0] out_234,
  output [7:0] out_235,
  output [7:0] out_236,
  output [7:0] out_237,
  output [7:0] out_238,
  output [7:0] out_239,
  output [7:0] out_240,
  output [7:0] out_241,
  output [7:0] out_242,
  output [7:0] out_243,
  output [7:0] out_244,
  output [7:0] out_245,
  output [7:0] out_246,
  output [7:0] out_247,
  output [7:0] out_248,
  output [7:0] out_249,
  output [7:0] out_250,
  output [7:0] out_251,
  output [7:0] out_252,
  output [7:0] out_253,
  output [7:0] out_254,
  output [7:0] out_255,
  output [7:0] out_256,
  output [7:0] out_257,
  output [7:0] out_258,
  output [7:0] out_259,
  output [7:0] out_260,
  output [7:0] out_261
);

  wire [7:0] undriven;
  wire [15:0] cpu_decoder_4x16_1_out_3, cpu_decoder_4x16_2_out_3;

  CPU_DECODER_4X16 cpu_decoder_4x16_1 (.out_3(cpu_decoder_4x16_1_out_3), .\input (address[7:4]));  // open: enable
  CPU_REG_BYTE cpu_reg_byte_1 (
    .reset(reset), .h(cpu_decoder_4x16_1_out_3[0]), .v(cpu_decoder_4x16_2_out_3[15]), .in_1(\input ),
    .\output (out_6), .s(set), .e(enable));
  CPU_REG_BYTE cpu_reg_byte_2 (
    .reset(reset), .h(cpu_decoder_4x16_1_out_3[1]), .v(cpu_decoder_4x16_2_out_3[15]), .in_1(\input ),
    .\output (out_22), .s(set), .e(enable));
  CPU_REG_BYTE cpu_reg_byte_3 (
    .reset(reset), .h(cpu_decoder_4x16_1_out_3[2]), .v(cpu_decoder_4x16_2_out_3[15]), .in_1(\input ),
    .\output (out_38), .s(set), .e(enable));
  CPU_REG_BYTE cpu_reg_byte_4 (
    .reset(reset), .h(cpu_decoder_4x16_1_out_3[3]), .v(cpu_decoder_4x16_2_out_3[15]), .in_1(\input ),
    .\output (out_54), .s(set), .e(enable));
  CPU_REG_BYTE cpu_reg_byte_5 (
    .reset(reset), .h(cpu_decoder_4x16_1_out_3[4]), .v(cpu_decoder_4x16_2_out_3[15]), .in_1(\input ),
    .\output (out_70), .s(set), .e(enable));
  CPU_REG_BYTE cpu_reg_byte_6 (
    .reset(reset), .h(cpu_decoder_4x16_1_out_3[5]), .v(cpu_decoder_4x16_2_out_3[15]), .in_1(\input ),
    .\output (out_86), .s(set), .e(enable));
  CPU_REG_BYTE cpu_reg_byte_7 (
    .reset(reset), .h(cpu_decoder_4x16_1_out_3[6]), .v(cpu_decoder_4x16_2_out_3[15]), .in_1(\input ),
    .\output (out_102), .s(set), .e(enable));
  CPU_REG_BYTE cpu_reg_byte_8 (
    .reset(reset), .h(cpu_decoder_4x16_1_out_3[7]), .v(cpu_decoder_4x16_2_out_3[15]), .in_1(\input ),
    .\output (out_118), .s(set), .e(enable));
  CPU_REG_BYTE cpu_reg_byte_9 (
    .reset(reset), .h(cpu_decoder_4x16_1_out_3[8]), .v(cpu_decoder_4x16_2_out_3[15]), .in_1(\input ),
    .\output (out_134), .s(set), .e(enable));
  CPU_REG_BYTE cpu_reg_byte_10 (
    .reset(reset), .h(cpu_decoder_4x16_1_out_3[9]), .v(cpu_decoder_4x16_2_out_3[15]), .in_1(\input ),
    .\output (out_150), .s(set), .e(enable));
  CPU_REG_BYTE cpu_reg_byte_11 (
    .reset(reset), .h(cpu_decoder_4x16_1_out_3[10]), .v(cpu_decoder_4x16_2_out_3[15]), .in_1(\input ),
    .\output (out_166), .s(set), .e(enable));
  CPU_REG_BYTE cpu_reg_byte_12 (
    .reset(reset), .h(cpu_decoder_4x16_1_out_3[11]), .v(cpu_decoder_4x16_2_out_3[15]), .in_1(\input ),
    .\output (out_182), .s(set), .e(enable));
  CPU_REG_BYTE cpu_reg_byte_13 (
    .reset(reset), .h(cpu_decoder_4x16_1_out_3[12]), .v(cpu_decoder_4x16_2_out_3[15]), .in_1(\input ),
    .\output (out_198), .s(set), .e(enable));
  CPU_REG_BYTE cpu_reg_byte_14 (
    .reset(reset), .h(cpu_decoder_4x16_1_out_3[13]), .v(cpu_decoder_4x16_2_out_3[15]), .in_1(undriven),
    .\output (out_214), .s(set), .e(enable));
  CPU_REG_BYTE cpu_reg_byte_15 (
    .reset(reset), .h(cpu_decoder_4x16_1_out_3[14]), .v(cpu_decoder_4x16_2_out_3[15]), .in_1(undriven),
    .\output (out_230), .s(set), .e(enable));
  CPU_REG_BYTE cpu_reg_byte_16 (
    .reset(reset), .h(cpu_decoder_4x16_1_out_3[15]), .v(cpu_decoder_4x16_2_out_3[15]), .in_1(undriven),
    .\output (out_246), .s(set), .e(enable));
  CPU_REG_BYTE cpu_reg_byte_17 (
    .reset(reset), .h(cpu_decoder_4x16_1_out_3[0]), .v(cpu_decoder_4x16_2_out_3[14]), .in_1(\input ),
    .\output (out_7), .s(set), .e(enable));
  CPU_REG_BYTE cpu_reg_byte_18 (
    .reset(reset), .h(cpu_decoder_4x16_1_out_3[1]), .v(cpu_decoder_4x16_2_out_3[14]), .in_1(\input ),
    .\output (out_23), .s(set), .e(enable));
  CPU_REG_BYTE cpu_reg_byte_19 (
    .reset(reset), .h(cpu_decoder_4x16_1_out_3[2]), .v(cpu_decoder_4x16_2_out_3[14]), .in_1(\input ),
    .\output (out_39), .s(set), .e(enable));
  CPU_REG_BYTE cpu_reg_byte_20 (
    .reset(reset), .h(cpu_decoder_4x16_1_out_3[3]), .v(cpu_decoder_4x16_2_out_3[14]), .in_1(\input ),
    .\output (out_55), .s(set), .e(enable));
  CPU_REG_BYTE cpu_reg_byte_21 (
    .reset(reset), .h(cpu_decoder_4x16_1_out_3[4]), .v(cpu_decoder_4x16_2_out_3[14]), .in_1(\input ),
    .\output (out_71), .s(set), .e(enable));
  CPU_REG_BYTE cpu_reg_byte_22 (
    .reset(reset), .h(cpu_decoder_4x16_1_out_3[5]), .v(cpu_decoder_4x16_2_out_3[14]), .in_1(\input ),
    .\output (out_87), .s(set), .e(enable));
  CPU_REG_BYTE cpu_reg_byte_23 (
    .reset(reset), .h(cpu_decoder_4x16_1_out_3[6]), .v(cpu_decoder_4x16_2_out_3[14]), .in_1(\input ),
    .\output (out_103), .s(set), .e(enable));
  CPU_REG_BYTE cpu_reg_byte_24 (
    .reset(reset), .h(cpu_decoder_4x16_1_out_3[7]), .v(cpu_decoder_4x16_2_out_3[14]), .in_1(\input ),
    .\output (out_119), .s(set), .e(enable));
  CPU_REG_BYTE cpu_reg_byte_25 (
    .reset(reset), .h(cpu_decoder_4x16_1_out_3[8]), .v(cpu_decoder_4x16_2_out_3[14]), .in_1(\input ),
    .\output (out_135), .s(set), .e(enable));
  CPU_REG_BYTE cpu_reg_byte_26 (
    .reset(reset), .h(cpu_decoder_4x16_1_out_3[9]), .v(cpu_decoder_4x16_2_out_3[14]), .in_1(\input ),
    .\output (out_151), .s(set), .e(enable));
  CPU_REG_BYTE cpu_reg_byte_27 (
    .reset(reset), .h(cpu_decoder_4x16_1_out_3[10]), .v(cpu_decoder_4x16_2_out_3[14]), .in_1(\input ),
    .\output (out_167), .s(set), .e(enable));
  CPU_REG_BYTE cpu_reg_byte_28 (
    .reset(reset), .h(cpu_decoder_4x16_1_out_3[11]), .v(cpu_decoder_4x16_2_out_3[14]), .in_1(\input ),
    .\output (out_183), .s(set), .e(enable));
  CPU_REG_BYTE cpu_reg_byte_29 (
    .reset(reset), .h(cpu_decoder_4x16_1_out_3[12]), .v(cpu_decoder_4x16_2_out_3[14]), .in_1(\input ),
    .\output (out_199), .s(set), .e(enable));
  CPU_REG_BYTE cpu_reg_byte_30 (
    .reset(reset), .h(cpu_decoder_4x16_1_out_3[13]), .v(cpu_decoder_4x16_2_out_3[14]), .in_1(undriven),
    .\output (out_215), .s(set), .e(enable));
  CPU_REG_BYTE cpu_reg_byte_31 (
    .reset(reset), .h(cpu_decoder_4x16_1_out_3[14]), .v(cpu_decoder_4x16_2_out_3[14]), .in_1(undriven),
    .\output (out_231), .s(set), .e(enable));
  CPU_REG_BYTE cpu_reg_byte_32 (
    .reset(reset), .h(cpu_decoder_4x16_1_out_3[15]), .v(cpu_decoder_4x16_2_out_3[14]), .in_1(undriven),
    .\output (out_247), .s(set), .e(enable));
  CPU_REG_BYTE cpu_reg_byte_33 (
    .reset(reset), .h(cpu_decoder_4x16_1_out_3[0]), .v(cpu_decoder_4x16_2_out_3[13]), .in_1(\input ),
    .\output (out_8), .s(set), .e(enable));
  CPU_REG_BYTE cpu_reg_byte_34 (
    .h(cpu_decoder_4x16_1_out_3[1]), .v(cpu_decoder_4x16_2_out_3[13]), .in_1(\input ), .\output (out_24),
    .s(set), .e(enable));  // open: reset
  CPU_REG_BYTE cpu_reg_byte_35 (
    .reset(reset), .h(cpu_decoder_4x16_1_out_3[2]), .v(cpu_decoder_4x16_2_out_3[13]), .in_1(\input ),
    .\output (out_40), .s(set), .e(enable));
  CPU_REG_BYTE cpu_reg_byte_36 (
    .reset(reset), .h(cpu_decoder_4x16_1_out_3[3]), .v(cpu_decoder_4x16_2_out_3[13]), .in_1(\input ),
    .\output (out_56), .s(set), .e(enable));
  CPU_REG_BYTE cpu_reg_byte_37 (
    .reset(reset), .h(cpu_decoder_4x16_1_out_3[4]), .v(cpu_decoder_4x16_2_out_3[13]), .in_1(\input ),
    .\output (out_72), .s(set), .e(enable));
  CPU_REG_BYTE cpu_reg_byte_38 (
    .reset(reset), .h(cpu_decoder_4x16_1_out_3[5]), .v(cpu_decoder_4x16_2_out_3[13]), .in_1(\input ),
    .\output (out_88), .s(set), .e(enable));
  CPU_REG_BYTE cpu_reg_byte_39 (
    .reset(reset), .h(cpu_decoder_4x16_1_out_3[6]), .v(cpu_decoder_4x16_2_out_3[13]), .in_1(\input ),
    .\output (out_104), .s(set), .e(enable));
  CPU_REG_BYTE cpu_reg_byte_40 (
    .reset(reset), .h(cpu_decoder_4x16_1_out_3[7]), .v(cpu_decoder_4x16_2_out_3[13]), .in_1(\input ),
    .\output (out_120), .s(set), .e(enable));
  CPU_REG_BYTE cpu_reg_byte_41 (
    .reset(reset), .h(cpu_decoder_4x16_1_out_3[8]), .v(cpu_decoder_4x16_2_out_3[13]), .in_1(\input ),
    .\output (out_136), .s(set), .e(enable));
  CPU_REG_BYTE cpu_reg_byte_42 (
    .reset(reset), .h(cpu_decoder_4x16_1_out_3[9]), .v(cpu_decoder_4x16_2_out_3[13]), .in_1(\input ),
    .\output (out_152), .s(set), .e(enable));
  CPU_REG_BYTE cpu_reg_byte_43 (
    .reset(reset), .h(cpu_decoder_4x16_1_out_3[10]), .v(cpu_decoder_4x16_2_out_3[13]), .in_1(\input ),
    .\output (out_168), .s(set), .e(enable));
  CPU_REG_BYTE cpu_reg_byte_44 (
    .reset(reset), .h(cpu_decoder_4x16_1_out_3[11]), .v(cpu_decoder_4x16_2_out_3[13]), .in_1(\input ),
    .\output (out_184), .s(set), .e(enable));
  CPU_REG_BYTE cpu_reg_byte_45 (
    .reset(reset), .h(cpu_decoder_4x16_1_out_3[12]), .v(cpu_decoder_4x16_2_out_3[13]), .in_1(\input ),
    .\output (out_200), .s(set), .e(enable));
  CPU_REG_BYTE cpu_reg_byte_46 (
    .reset(reset), .h(cpu_decoder_4x16_1_out_3[13]), .v(cpu_decoder_4x16_2_out_3[13]), .in_1(undriven),
    .\output (out_216), .s(set), .e(enable));
  CPU_REG_BYTE cpu_reg_byte_47 (
    .reset(reset), .h(cpu_decoder_4x16_1_out_3[14]), .v(cpu_decoder_4x16_2_out_3[13]), .in_1(undriven),
    .\output (out_232), .s(set), .e(enable));
  CPU_REG_BYTE cpu_reg_byte_48 (
    .reset(reset), .h(cpu_decoder_4x16_1_out_3[15]), .v(cpu_decoder_4x16_2_out_3[13]), .in_1(undriven),
    .\output (out_248), .s(set), .e(enable));
  CPU_DECODER_4X16 cpu_decoder_4x16_2 (.out_3(cpu_decoder_4x16_2_out_3), .\input (address[3:0]));  // open: enable
  CPU_REG_BYTE cpu_reg_byte_49 (
    .reset(reset), .h(cpu_decoder_4x16_1_out_3[0]), .v(cpu_decoder_4x16_2_out_3[12]), .in_1(\input ),
    .\output (out_9), .s(set), .e(enable));
  CPU_REG_BYTE cpu_reg_byte_50 (
    .reset(reset), .h(cpu_decoder_4x16_1_out_3[1]), .v(cpu_decoder_4x16_2_out_3[12]), .in_1(\input ),
    .\output (out_25), .s(set), .e(enable));
  CPU_REG_BYTE cpu_reg_byte_51 (
    .reset(reset), .h(cpu_decoder_4x16_1_out_3[2]), .v(cpu_decoder_4x16_2_out_3[12]), .in_1(\input ),
    .\output (out_41), .s(set), .e(enable));
  CPU_REG_BYTE cpu_reg_byte_52 (
    .reset(reset), .h(cpu_decoder_4x16_1_out_3[3]), .v(cpu_decoder_4x16_2_out_3[12]), .in_1(\input ),
    .\output (out_57), .s(set), .e(enable));
  CPU_REG_BYTE cpu_reg_byte_53 (
    .reset(reset), .h(cpu_decoder_4x16_1_out_3[4]), .v(cpu_decoder_4x16_2_out_3[12]), .in_1(\input ),
    .\output (out_73), .s(set), .e(enable));
  CPU_REG_BYTE cpu_reg_byte_54 (
    .reset(reset), .h(cpu_decoder_4x16_1_out_3[5]), .v(cpu_decoder_4x16_2_out_3[12]), .in_1(\input ),
    .\output (out_89), .s(set), .e(enable));
  CPU_REG_BYTE cpu_reg_byte_55 (
    .reset(reset), .h(cpu_decoder_4x16_1_out_3[6]), .v(cpu_decoder_4x16_2_out_3[12]), .in_1(\input ),
    .\output (out_105), .s(set), .e(enable));
  CPU_REG_BYTE cpu_reg_byte_56 (
    .reset(reset), .h(cpu_decoder_4x16_1_out_3[7]), .v(cpu_decoder_4x16_2_out_3[12]), .in_1(\input ),
    .\output (out_121), .s(set), .e(enable));
  CPU_REG_BYTE cpu_reg_byte_57 (
    .reset(reset), .h(cpu_decoder_4x16_1_out_3[8]), .v(cpu_decoder_4x16_2_out_3[12]), .in_1(\input ),
    .\output (out_137), .s(set), .e(enable));
  CPU_REG_BYTE cpu_reg_byte_58 (
    .reset(reset), .h(cpu_decoder_4x16_1_out_3[9]), .v(cpu_decoder_4x16_2_out_3[12]), .in_1(\input ),
    .\output (out_153), .s(set), .e(enable));
  CPU_REG_BYTE cpu_reg_byte_59 (
    .reset(reset), .h(cpu_decoder_4x16_1_out_3[10]), .v(cpu_decoder_4x16_2_out_3[12]), .in_1(\input ),
    .\output (out_169), .s(set), .e(enable));
  CPU_REG_BYTE cpu_reg_byte_60 (
    .reset(reset), .h(cpu_decoder_4x16_1_out_3[11]), .v(cpu_decoder_4x16_2_out_3[12]), .in_1(\input ),
    .\output (out_185), .s(set), .e(enable));
  CPU_REG_BYTE cpu_reg_byte_61 (
    .reset(reset), .h(cpu_decoder_4x16_1_out_3[12]), .v(cpu_decoder_4x16_2_out_3[12]), .in_1(\input ),
    .\output (out_201), .s(set), .e(enable));
  CPU_REG_BYTE cpu_reg_byte_62 (
    .reset(reset), .h(cpu_decoder_4x16_1_out_3[13]), .v(cpu_decoder_4x16_2_out_3[12]), .in_1(undriven),
    .\output (out_217), .s(set), .e(enable));
  CPU_REG_BYTE cpu_reg_byte_63 (
    .reset(reset), .h(cpu_decoder_4x16_1_out_3[14]), .v(cpu_decoder_4x16_2_out_3[12]), .in_1(undriven),
    .\output (out_233), .s(set), .e(enable));
  CPU_REG_BYTE cpu_reg_byte_64 (
    .reset(reset), .h(cpu_decoder_4x16_1_out_3[15]), .v(cpu_decoder_4x16_2_out_3[12]), .in_1(undriven),
    .\output (out_249), .s(set), .e(enable));
  CPU_REG_BYTE cpu_reg_byte_65 (
    .reset(reset), .h(cpu_decoder_4x16_1_out_3[0]), .v(cpu_decoder_4x16_2_out_3[11]), .in_1(\input ),
    .\output (out_10), .s(set), .e(enable));
  CPU_REG_BYTE cpu_reg_byte_66 (
    .reset(reset), .h(cpu_decoder_4x16_1_out_3[1]), .v(cpu_decoder_4x16_2_out_3[11]), .in_1(\input ),
    .\output (out_26), .s(set), .e(enable));
  CPU_REG_BYTE cpu_reg_byte_67 (
    .reset(reset), .h(cpu_decoder_4x16_1_out_3[2]), .v(cpu_decoder_4x16_2_out_3[11]), .in_1(\input ),
    .\output (out_42), .s(set), .e(enable));
  CPU_REG_BYTE cpu_reg_byte_68 (
    .reset(reset), .h(cpu_decoder_4x16_1_out_3[3]), .v(cpu_decoder_4x16_2_out_3[11]), .in_1(\input ),
    .\output (out_58), .s(set), .e(enable));
  CPU_REG_BYTE cpu_reg_byte_69 (
    .reset(reset), .h(cpu_decoder_4x16_1_out_3[4]), .v(cpu_decoder_4x16_2_out_3[11]), .in_1(\input ),
    .\output (out_74), .s(set), .e(enable));
  CPU_REG_BYTE cpu_reg_byte_70 (
    .reset(reset), .h(cpu_decoder_4x16_1_out_3[5]), .v(cpu_decoder_4x16_2_out_3[11]), .in_1(\input ),
    .\output (out_90), .s(set), .e(enable));
  CPU_REG_BYTE cpu_reg_byte_71 (
    .reset(reset), .h(cpu_decoder_4x16_1_out_3[6]), .v(cpu_decoder_4x16_2_out_3[11]), .in_1(\input ),
    .\output (out_106), .s(set), .e(enable));
  CPU_REG_BYTE cpu_reg_byte_72 (
    .reset(reset), .h(cpu_decoder_4x16_1_out_3[7]), .v(cpu_decoder_4x16_2_out_3[11]), .in_1(\input ),
    .\output (out_122), .s(set), .e(enable));
  CPU_REG_BYTE cpu_reg_byte_73 (
    .reset(reset), .h(cpu_decoder_4x16_1_out_3[8]), .v(cpu_decoder_4x16_2_out_3[11]), .in_1(\input ),
    .\output (out_138), .s(set), .e(enable));
  CPU_REG_BYTE cpu_reg_byte_74 (
    .reset(reset), .h(cpu_decoder_4x16_1_out_3[9]), .v(cpu_decoder_4x16_2_out_3[11]), .in_1(\input ),
    .\output (out_154), .s(set), .e(enable));
  CPU_REG_BYTE cpu_reg_byte_75 (
    .reset(reset), .h(cpu_decoder_4x16_1_out_3[10]), .v(cpu_decoder_4x16_2_out_3[11]), .in_1(\input ),
    .\output (out_170), .s(set), .e(enable));
  CPU_REG_BYTE cpu_reg_byte_76 (
    .reset(reset), .h(cpu_decoder_4x16_1_out_3[11]), .v(cpu_decoder_4x16_2_out_3[11]), .in_1(\input ),
    .\output (out_186), .s(set), .e(enable));
  CPU_REG_BYTE cpu_reg_byte_77 (
    .reset(reset), .h(cpu_decoder_4x16_1_out_3[12]), .v(cpu_decoder_4x16_2_out_3[11]), .in_1(\input ),
    .\output (out_202), .s(set), .e(enable));
  CPU_REG_BYTE cpu_reg_byte_78 (
    .reset(reset), .h(cpu_decoder_4x16_1_out_3[13]), .v(cpu_decoder_4x16_2_out_3[11]), .in_1(undriven),
    .\output (out_218), .s(set), .e(enable));
  CPU_REG_BYTE cpu_reg_byte_79 (
    .reset(reset), .h(cpu_decoder_4x16_1_out_3[14]), .v(cpu_decoder_4x16_2_out_3[11]), .in_1(undriven),
    .\output (out_234), .s(set), .e(enable));
  CPU_REG_BYTE cpu_reg_byte_80 (
    .reset(reset), .h(cpu_decoder_4x16_1_out_3[15]), .v(cpu_decoder_4x16_2_out_3[11]), .in_1(undriven),
    .\output (out_250), .s(set), .e(enable));
  CPU_REG_BYTE cpu_reg_byte_81 (
    .reset(reset), .h(cpu_decoder_4x16_1_out_3[0]), .v(cpu_decoder_4x16_2_out_3[10]), .\output (out_11),
    .s(set), .e(enable));  // open: in_1
  CPU_REG_BYTE cpu_reg_byte_82 (
    .reset(reset), .h(cpu_decoder_4x16_1_out_3[1]), .v(cpu_decoder_4x16_2_out_3[10]), .in_1(\input ),
    .\output (out_27), .s(set), .e(enable));
  CPU_REG_BYTE cpu_reg_byte_83 (
    .reset(reset), .h(cpu_decoder_4x16_1_out_3[2]), .v(cpu_decoder_4x16_2_out_3[10]), .in_1(\input ),
    .\output (out_43), .s(set), .e(enable));
  CPU_REG_BYTE cpu_reg_byte_84 (
    .reset(reset), .h(cpu_decoder_4x16_1_out_3[3]), .v(cpu_decoder_4x16_2_out_3[10]), .in_1(\input ),
    .\output (out_59), .s(set), .e(enable));
  CPU_REG_BYTE cpu_reg_byte_85 (
    .reset(reset), .h(cpu_decoder_4x16_1_out_3[4]), .v(cpu_decoder_4x16_2_out_3[10]), .in_1(\input ),
    .\output (out_75), .s(set), .e(enable));
  CPU_REG_BYTE cpu_reg_byte_86 (
    .reset(reset), .h(cpu_decoder_4x16_1_out_3[5]), .v(cpu_decoder_4x16_2_out_3[10]), .in_1(\input ),
    .\output (out_91), .s(set), .e(enable));
  CPU_REG_BYTE cpu_reg_byte_87 (
    .reset(reset), .h(cpu_decoder_4x16_1_out_3[6]), .v(cpu_decoder_4x16_2_out_3[10]), .in_1(\input ),
    .\output (out_107), .s(set), .e(enable));
  CPU_REG_BYTE cpu_reg_byte_88 (
    .reset(reset), .h(cpu_decoder_4x16_1_out_3[7]), .v(cpu_decoder_4x16_2_out_3[10]), .in_1(\input ),
    .\output (out_123), .s(set), .e(enable));
  CPU_REG_BYTE cpu_reg_byte_89 (
    .reset(reset), .h(cpu_decoder_4x16_1_out_3[8]), .v(cpu_decoder_4x16_2_out_3[10]), .in_1(\input ),
    .\output (out_139), .s(set), .e(enable));
  CPU_REG_BYTE cpu_reg_byte_90 (
    .reset(reset), .h(cpu_decoder_4x16_1_out_3[9]), .v(cpu_decoder_4x16_2_out_3[10]), .in_1(\input ),
    .\output (out_155), .s(set), .e(enable));
  CPU_REG_BYTE cpu_reg_byte_91 (
    .reset(reset), .h(cpu_decoder_4x16_1_out_3[10]), .v(cpu_decoder_4x16_2_out_3[10]), .in_1(\input ),
    .\output (out_171), .s(set), .e(enable));
  CPU_REG_BYTE cpu_reg_byte_92 (
    .reset(reset), .h(cpu_decoder_4x16_1_out_3[11]), .v(cpu_decoder_4x16_2_out_3[10]), .in_1(\input ),
    .\output (out_187), .s(set), .e(enable));
  CPU_REG_BYTE cpu_reg_byte_93 (
    .reset(reset), .h(cpu_decoder_4x16_1_out_3[12]), .v(cpu_decoder_4x16_2_out_3[10]), .in_1(\input ),
    .\output (out_203), .s(set), .e(enable));
  CPU_REG_BYTE cpu_reg_byte_94 (
    .reset(reset), .h(cpu_decoder_4x16_1_out_3[13]), .v(cpu_decoder_4x16_2_out_3[10]), .in_1(undriven),
    .\output (out_219), .s(set), .e(enable));
  CPU_REG_BYTE cpu_reg_byte_95 (
    .reset(reset), .h(cpu_decoder_4x16_1_out_3[14]), .v(cpu_decoder_4x16_2_out_3[10]), .in_1(undriven),
    .\output (out_235), .s(set), .e(enable));
  CPU_REG_BYTE cpu_reg_byte_96 (
    .reset(reset), .h(cpu_decoder_4x16_1_out_3[15]), .v(cpu_decoder_4x16_2_out_3[10]), .in_1(undriven),
    .\output (out_251), .s(set), .e(enable));
  CPU_REG_BYTE cpu_reg_byte_97 (
    .reset(reset), .h(cpu_decoder_4x16_1_out_3[0]), .v(cpu_decoder_4x16_2_out_3[9]), .in_1(\input ),
    .\output (out_12), .s(set), .e(enable));
  CPU_REG_BYTE cpu_reg_byte_98 (
    .h(cpu_decoder_4x16_1_out_3[1]), .v(cpu_decoder_4x16_2_out_3[9]), .in_1(\input ), .\output (out_28),
    .s(set), .e(enable));  // open: reset
  CPU_REG_BYTE cpu_reg_byte_99 (
    .reset(reset), .h(cpu_decoder_4x16_1_out_3[2]), .v(cpu_decoder_4x16_2_out_3[9]), .in_1(\input ),
    .\output (out_44), .s(set), .e(enable));
  CPU_REG_BYTE cpu_reg_byte_100 (
    .reset(reset), .h(cpu_decoder_4x16_1_out_3[3]), .v(cpu_decoder_4x16_2_out_3[9]), .in_1(\input ),
    .\output (out_60), .s(set), .e(enable));
  CPU_REG_BYTE cpu_reg_byte_101 (
    .reset(reset), .h(cpu_decoder_4x16_1_out_3[4]), .v(cpu_decoder_4x16_2_out_3[9]), .in_1(\input ),
    .\output (out_76), .s(set), .e(enable));
  CPU_REG_BYTE cpu_reg_byte_102 (
    .reset(reset), .h(cpu_decoder_4x16_1_out_3[5]), .v(cpu_decoder_4x16_2_out_3[9]), .in_1(\input ),
    .\output (out_92), .s(set), .e(enable));
  CPU_REG_BYTE cpu_reg_byte_103 (
    .reset(reset), .h(cpu_decoder_4x16_1_out_3[6]), .v(cpu_decoder_4x16_2_out_3[9]), .in_1(\input ),
    .\output (out_108), .s(set), .e(enable));
  CPU_REG_BYTE cpu_reg_byte_104 (
    .reset(reset), .h(cpu_decoder_4x16_1_out_3[7]), .v(cpu_decoder_4x16_2_out_3[9]), .in_1(\input ),
    .\output (out_124), .s(set), .e(enable));
  CPU_REG_BYTE cpu_reg_byte_105 (
    .reset(reset), .h(cpu_decoder_4x16_1_out_3[8]), .v(cpu_decoder_4x16_2_out_3[9]), .in_1(\input ),
    .\output (out_140), .s(set), .e(enable));
  CPU_REG_BYTE cpu_reg_byte_106 (
    .reset(reset), .h(cpu_decoder_4x16_1_out_3[9]), .v(cpu_decoder_4x16_2_out_3[9]), .in_1(\input ),
    .\output (out_156), .s(set), .e(enable));
  CPU_REG_BYTE cpu_reg_byte_107 (
    .reset(reset), .h(cpu_decoder_4x16_1_out_3[10]), .v(cpu_decoder_4x16_2_out_3[9]), .in_1(\input ),
    .\output (out_172), .s(set), .e(enable));
  CPU_REG_BYTE cpu_reg_byte_108 (
    .reset(reset), .h(cpu_decoder_4x16_1_out_3[11]), .v(cpu_decoder_4x16_2_out_3[9]), .in_1(\input ),
    .\output (out_188), .s(set), .e(enable));
  CPU_REG_BYTE cpu_reg_byte_109 (
    .reset(reset), .h(cpu_decoder_4x16_1_out_3[12]), .v(cpu_decoder_4x16_2_out_3[9]), .in_1(\input ),
    .\output (out_204), .s(set), .e(enable));
  CPU_REG_BYTE cpu_reg_byte_110 (
    .reset(reset), .h(cpu_decoder_4x16_1_out_3[13]), .v(cpu_decoder_4x16_2_out_3[9]), .in_1(undriven),
    .\output (out_220), .s(set), .e(enable));
  CPU_REG_BYTE cpu_reg_byte_111 (
    .reset(reset), .h(cpu_decoder_4x16_1_out_3[14]), .v(cpu_decoder_4x16_2_out_3[9]), .in_1(undriven),
    .\output (out_236), .s(set), .e(enable));
  CPU_REG_BYTE cpu_reg_byte_112 (
    .reset(reset), .h(cpu_decoder_4x16_1_out_3[15]), .v(cpu_decoder_4x16_2_out_3[9]), .in_1(undriven),
    .\output (out_252), .s(set), .e(enable));
  CPU_REG_BYTE cpu_reg_byte_113 (
    .reset(reset), .h(cpu_decoder_4x16_1_out_3[0]), .v(cpu_decoder_4x16_2_out_3[8]), .in_1(\input ),
    .\output (out_13), .s(set), .e(enable));
  CPU_REG_BYTE cpu_reg_byte_114 (
    .reset(reset), .h(cpu_decoder_4x16_1_out_3[1]), .v(cpu_decoder_4x16_2_out_3[8]), .in_1(\input ),
    .\output (out_29), .s(set), .e(enable));
  CPU_REG_BYTE cpu_reg_byte_115 (
    .reset(reset), .h(cpu_decoder_4x16_1_out_3[2]), .v(cpu_decoder_4x16_2_out_3[8]), .in_1(\input ),
    .\output (out_45), .s(set), .e(enable));
  CPU_REG_BYTE cpu_reg_byte_116 (
    .reset(reset), .h(cpu_decoder_4x16_1_out_3[3]), .v(cpu_decoder_4x16_2_out_3[8]), .in_1(\input ),
    .\output (out_61), .s(set), .e(enable));
  CPU_REG_BYTE cpu_reg_byte_117 (
    .reset(reset), .h(cpu_decoder_4x16_1_out_3[4]), .v(cpu_decoder_4x16_2_out_3[8]), .in_1(\input ),
    .\output (out_77), .s(set), .e(enable));
  CPU_REG_BYTE cpu_reg_byte_118 (
    .reset(reset), .h(cpu_decoder_4x16_1_out_3[5]), .v(cpu_decoder_4x16_2_out_3[8]), .in_1(\input ),
    .\output (out_93), .s(set), .e(enable));
  CPU_REG_BYTE cpu_reg_byte_119 (
    .reset(reset), .h(cpu_decoder_4x16_1_out_3[6]), .v(cpu_decoder_4x16_2_out_3[8]), .in_1(\input ),
    .\output (out_109), .s(set), .e(enable));
  CPU_REG_BYTE cpu_reg_byte_120 (
    .reset(reset), .h(cpu_decoder_4x16_1_out_3[7]), .v(cpu_decoder_4x16_2_out_3[8]), .in_1(\input ),
    .\output (out_125), .s(set), .e(enable));
  CPU_REG_BYTE cpu_reg_byte_121 (
    .reset(reset), .h(cpu_decoder_4x16_1_out_3[8]), .v(cpu_decoder_4x16_2_out_3[8]), .in_1(\input ),
    .\output (out_141), .s(set), .e(enable));
  CPU_REG_BYTE cpu_reg_byte_122 (
    .reset(reset), .h(cpu_decoder_4x16_1_out_3[9]), .v(cpu_decoder_4x16_2_out_3[8]), .in_1(\input ),
    .\output (out_157), .s(set), .e(enable));
  CPU_REG_BYTE cpu_reg_byte_123 (
    .reset(reset), .h(cpu_decoder_4x16_1_out_3[10]), .v(cpu_decoder_4x16_2_out_3[8]), .in_1(\input ),
    .\output (out_173), .s(set), .e(enable));
  CPU_REG_BYTE cpu_reg_byte_124 (
    .reset(reset), .h(cpu_decoder_4x16_1_out_3[11]), .v(cpu_decoder_4x16_2_out_3[8]), .in_1(\input ),
    .\output (out_189), .s(set), .e(enable));
  CPU_REG_BYTE cpu_reg_byte_125 (
    .reset(reset), .h(cpu_decoder_4x16_1_out_3[12]), .v(cpu_decoder_4x16_2_out_3[8]), .in_1(\input ),
    .\output (out_205), .s(set), .e(enable));
  CPU_REG_BYTE cpu_reg_byte_126 (
    .reset(reset), .h(cpu_decoder_4x16_1_out_3[13]), .v(cpu_decoder_4x16_2_out_3[8]), .in_1(undriven),
    .\output (out_221), .s(set), .e(enable));
  CPU_REG_BYTE cpu_reg_byte_127 (
    .reset(reset), .h(cpu_decoder_4x16_1_out_3[14]), .v(cpu_decoder_4x16_2_out_3[8]), .in_1(undriven),
    .\output (out_237), .s(set), .e(enable));
  CPU_REG_BYTE cpu_reg_byte_128 (
    .reset(reset), .h(cpu_decoder_4x16_1_out_3[15]), .v(cpu_decoder_4x16_2_out_3[8]), .in_1(undriven),
    .\output (out_253), .s(set), .e(enable));
  CPU_REG_BYTE cpu_reg_byte_129 (
    .reset(reset), .h(cpu_decoder_4x16_1_out_3[0]), .v(cpu_decoder_4x16_2_out_3[7]), .in_1(\input ),
    .\output (out_14), .s(set), .e(enable));
  CPU_REG_BYTE cpu_reg_byte_130 (
    .reset(reset), .h(cpu_decoder_4x16_1_out_3[1]), .v(cpu_decoder_4x16_2_out_3[7]), .in_1(\input ),
    .\output (out_30), .s(set), .e(enable));
  CPU_REG_BYTE cpu_reg_byte_131 (
    .reset(reset), .h(cpu_decoder_4x16_1_out_3[2]), .v(cpu_decoder_4x16_2_out_3[7]), .in_1(\input ),
    .\output (out_46), .s(set), .e(enable));
  CPU_REG_BYTE cpu_reg_byte_132 (
    .reset(reset), .h(cpu_decoder_4x16_1_out_3[3]), .v(cpu_decoder_4x16_2_out_3[7]), .in_1(\input ),
    .\output (out_62), .s(set), .e(enable));
  CPU_REG_BYTE cpu_reg_byte_133 (
    .reset(reset), .h(cpu_decoder_4x16_1_out_3[4]), .v(cpu_decoder_4x16_2_out_3[7]), .in_1(\input ),
    .\output (out_78), .s(set), .e(enable));
  CPU_REG_BYTE cpu_reg_byte_134 (
    .reset(reset), .h(cpu_decoder_4x16_1_out_3[5]), .v(cpu_decoder_4x16_2_out_3[7]), .in_1(\input ),
    .\output (out_94), .s(set), .e(enable));
  CPU_REG_BYTE cpu_reg_byte_135 (
    .reset(reset), .h(cpu_decoder_4x16_1_out_3[6]), .v(cpu_decoder_4x16_2_out_3[7]), .in_1(\input ),
    .\output (out_110), .s(set), .e(enable));
  CPU_REG_BYTE cpu_reg_byte_136 (
    .reset(reset), .h(cpu_decoder_4x16_1_out_3[7]), .v(cpu_decoder_4x16_2_out_3[7]), .in_1(\input ),
    .\output (out_126), .s(set), .e(enable));
  CPU_REG_BYTE cpu_reg_byte_137 (
    .reset(reset), .h(cpu_decoder_4x16_1_out_3[8]), .v(cpu_decoder_4x16_2_out_3[7]), .in_1(\input ),
    .\output (out_142), .s(set), .e(enable));
  CPU_REG_BYTE cpu_reg_byte_138 (
    .reset(reset), .h(cpu_decoder_4x16_1_out_3[9]), .v(cpu_decoder_4x16_2_out_3[7]), .in_1(\input ),
    .\output (out_158), .s(set), .e(enable));
  CPU_REG_BYTE cpu_reg_byte_139 (
    .reset(reset), .h(cpu_decoder_4x16_1_out_3[10]), .v(cpu_decoder_4x16_2_out_3[7]), .in_1(\input ),
    .\output (out_174), .s(set), .e(enable));
  CPU_REG_BYTE cpu_reg_byte_140 (
    .reset(reset), .h(cpu_decoder_4x16_1_out_3[11]), .v(cpu_decoder_4x16_2_out_3[7]), .in_1(\input ),
    .\output (out_190), .s(set), .e(enable));
  CPU_REG_BYTE cpu_reg_byte_141 (
    .reset(reset), .h(cpu_decoder_4x16_1_out_3[12]), .v(cpu_decoder_4x16_2_out_3[7]), .in_1(\input ),
    .\output (out_206), .s(set), .e(enable));
  CPU_REG_BYTE cpu_reg_byte_142 (
    .reset(reset), .h(cpu_decoder_4x16_1_out_3[13]), .v(cpu_decoder_4x16_2_out_3[7]), .in_1(undriven),
    .\output (out_222), .s(set), .e(enable));
  CPU_REG_BYTE cpu_reg_byte_143 (
    .reset(reset), .h(cpu_decoder_4x16_1_out_3[14]), .v(cpu_decoder_4x16_2_out_3[7]), .in_1(undriven),
    .\output (out_238), .s(set), .e(enable));
  CPU_REG_BYTE cpu_reg_byte_144 (
    .reset(reset), .h(cpu_decoder_4x16_1_out_3[15]), .v(cpu_decoder_4x16_2_out_3[7]), .in_1(undriven),
    .\output (out_254), .s(set), .e(enable));
  CPU_REG_BYTE cpu_reg_byte_145 (
    .reset(reset), .h(cpu_decoder_4x16_1_out_3[0]), .v(cpu_decoder_4x16_2_out_3[6]), .in_1(\input ),
    .\output (out_15), .s(set), .e(enable));
  CPU_REG_BYTE cpu_reg_byte_146 (
    .reset(reset), .h(cpu_decoder_4x16_1_out_3[1]), .v(cpu_decoder_4x16_2_out_3[6]), .in_1(\input ),
    .\output (out_31), .s(set), .e(enable));
  CPU_REG_BYTE cpu_reg_byte_147 (
    .reset(reset), .h(cpu_decoder_4x16_1_out_3[2]), .v(cpu_decoder_4x16_2_out_3[6]), .in_1(\input ),
    .\output (out_47), .s(set), .e(enable));
  CPU_REG_BYTE cpu_reg_byte_148 (
    .reset(reset), .h(cpu_decoder_4x16_1_out_3[3]), .v(cpu_decoder_4x16_2_out_3[6]), .in_1(\input ),
    .\output (out_63), .s(set), .e(enable));
  CPU_REG_BYTE cpu_reg_byte_149 (
    .reset(reset), .h(cpu_decoder_4x16_1_out_3[4]), .v(cpu_decoder_4x16_2_out_3[6]), .in_1(\input ),
    .\output (out_79), .s(set), .e(enable));
  CPU_REG_BYTE cpu_reg_byte_150 (
    .reset(reset), .h(cpu_decoder_4x16_1_out_3[5]), .v(cpu_decoder_4x16_2_out_3[6]), .in_1(\input ),
    .\output (out_95), .s(set), .e(enable));
  CPU_REG_BYTE cpu_reg_byte_151 (
    .reset(reset), .h(cpu_decoder_4x16_1_out_3[6]), .v(cpu_decoder_4x16_2_out_3[6]), .in_1(\input ),
    .\output (out_111), .s(set), .e(enable));
  CPU_REG_BYTE cpu_reg_byte_152 (
    .reset(reset), .h(cpu_decoder_4x16_1_out_3[7]), .v(cpu_decoder_4x16_2_out_3[6]), .in_1(\input ),
    .\output (out_127), .s(set), .e(enable));
  CPU_REG_BYTE cpu_reg_byte_153 (
    .reset(reset), .h(cpu_decoder_4x16_1_out_3[8]), .v(cpu_decoder_4x16_2_out_3[6]), .in_1(\input ),
    .\output (out_143), .s(set), .e(enable));
  CPU_REG_BYTE cpu_reg_byte_154 (
    .reset(reset), .h(cpu_decoder_4x16_1_out_3[9]), .v(cpu_decoder_4x16_2_out_3[6]), .in_1(\input ),
    .\output (out_159), .s(set), .e(enable));
  CPU_REG_BYTE cpu_reg_byte_155 (
    .reset(reset), .h(cpu_decoder_4x16_1_out_3[10]), .v(cpu_decoder_4x16_2_out_3[6]), .in_1(\input ),
    .\output (out_175), .s(set), .e(enable));
  CPU_REG_BYTE cpu_reg_byte_156 (
    .reset(reset), .h(cpu_decoder_4x16_1_out_3[11]), .v(cpu_decoder_4x16_2_out_3[6]), .in_1(\input ),
    .\output (out_191), .s(set), .e(enable));
  CPU_REG_BYTE cpu_reg_byte_157 (
    .reset(reset), .h(cpu_decoder_4x16_1_out_3[12]), .v(cpu_decoder_4x16_2_out_3[6]), .in_1(\input ),
    .\output (out_207), .s(set), .e(enable));
  CPU_REG_BYTE cpu_reg_byte_158 (
    .reset(reset), .h(cpu_decoder_4x16_1_out_3[13]), .v(cpu_decoder_4x16_2_out_3[6]), .in_1(undriven),
    .\output (out_223), .s(set), .e(enable));
  CPU_REG_BYTE cpu_reg_byte_159 (
    .reset(reset), .h(cpu_decoder_4x16_1_out_3[14]), .v(cpu_decoder_4x16_2_out_3[6]), .in_1(undriven),
    .\output (out_239), .s(set), .e(enable));
  CPU_REG_BYTE cpu_reg_byte_160 (
    .reset(reset), .h(cpu_decoder_4x16_1_out_3[15]), .v(cpu_decoder_4x16_2_out_3[6]), .in_1(undriven),
    .\output (out_255), .s(set), .e(enable));
  CPU_REG_BYTE cpu_reg_byte_161 (
    .reset(reset), .h(cpu_decoder_4x16_1_out_3[0]), .v(cpu_decoder_4x16_2_out_3[5]), .in_1(\input ),
    .\output (out_16), .s(set), .e(enable));
  CPU_REG_BYTE cpu_reg_byte_162 (
    .h(cpu_decoder_4x16_1_out_3[1]), .v(cpu_decoder_4x16_2_out_3[5]), .in_1(\input ), .\output (out_32),
    .s(set), .e(enable));  // open: reset
  CPU_REG_BYTE cpu_reg_byte_163 (
    .reset(reset), .h(cpu_decoder_4x16_1_out_3[2]), .v(cpu_decoder_4x16_2_out_3[5]), .in_1(\input ),
    .\output (out_48), .s(set), .e(enable));
  CPU_REG_BYTE cpu_reg_byte_164 (
    .reset(reset), .h(cpu_decoder_4x16_1_out_3[3]), .v(cpu_decoder_4x16_2_out_3[5]), .in_1(\input ),
    .\output (out_64), .s(set), .e(enable));
  CPU_REG_BYTE cpu_reg_byte_165 (
    .reset(reset), .h(cpu_decoder_4x16_1_out_3[4]), .v(cpu_decoder_4x16_2_out_3[5]), .in_1(\input ),
    .\output (out_80), .s(set), .e(enable));
  CPU_REG_BYTE cpu_reg_byte_166 (
    .reset(reset), .h(cpu_decoder_4x16_1_out_3[5]), .v(cpu_decoder_4x16_2_out_3[5]), .in_1(\input ),
    .\output (out_96), .s(set), .e(enable));
  CPU_REG_BYTE cpu_reg_byte_167 (
    .reset(reset), .h(cpu_decoder_4x16_1_out_3[6]), .v(cpu_decoder_4x16_2_out_3[5]), .in_1(\input ),
    .\output (out_112), .s(set), .e(enable));
  CPU_REG_BYTE cpu_reg_byte_168 (
    .reset(reset), .h(cpu_decoder_4x16_1_out_3[7]), .v(cpu_decoder_4x16_2_out_3[5]), .in_1(\input ),
    .\output (out_128), .s(set), .e(enable));
  CPU_REG_BYTE cpu_reg_byte_169 (
    .reset(reset), .h(cpu_decoder_4x16_1_out_3[8]), .v(cpu_decoder_4x16_2_out_3[5]), .in_1(\input ),
    .\output (out_144), .s(set), .e(enable));
  CPU_REG_BYTE cpu_reg_byte_170 (
    .reset(reset), .h(cpu_decoder_4x16_1_out_3[9]), .v(cpu_decoder_4x16_2_out_3[5]), .in_1(\input ),
    .\output (out_160), .s(set), .e(enable));
  CPU_REG_BYTE cpu_reg_byte_171 (
    .reset(reset), .h(cpu_decoder_4x16_1_out_3[10]), .v(cpu_decoder_4x16_2_out_3[5]), .in_1(\input ),
    .\output (out_176), .s(set), .e(enable));
  CPU_REG_BYTE cpu_reg_byte_172 (
    .reset(reset), .h(cpu_decoder_4x16_1_out_3[11]), .v(cpu_decoder_4x16_2_out_3[5]), .in_1(\input ),
    .\output (out_192), .s(set), .e(enable));
  CPU_REG_BYTE cpu_reg_byte_173 (
    .reset(reset), .h(cpu_decoder_4x16_1_out_3[12]), .v(cpu_decoder_4x16_2_out_3[5]), .in_1(\input ),
    .\output (out_208), .s(set), .e(enable));
  CPU_REG_BYTE cpu_reg_byte_174 (
    .reset(reset), .h(cpu_decoder_4x16_1_out_3[13]), .v(cpu_decoder_4x16_2_out_3[5]), .in_1(undriven),
    .\output (out_224), .s(set), .e(enable));
  CPU_REG_BYTE cpu_reg_byte_175 (
    .reset(reset), .h(cpu_decoder_4x16_1_out_3[14]), .v(cpu_decoder_4x16_2_out_3[5]), .in_1(undriven),
    .\output (out_240), .s(set), .e(enable));
  CPU_REG_BYTE cpu_reg_byte_176 (
    .reset(reset), .h(cpu_decoder_4x16_1_out_3[15]), .v(cpu_decoder_4x16_2_out_3[5]), .in_1(undriven),
    .\output (out_256), .s(set), .e(enable));
  CPU_REG_BYTE cpu_reg_byte_177 (
    .reset(reset), .h(cpu_decoder_4x16_1_out_3[0]), .v(cpu_decoder_4x16_2_out_3[4]), .in_1(\input ),
    .\output (out_17), .s(set), .e(enable));
  CPU_REG_BYTE cpu_reg_byte_178 (
    .reset(reset), .h(cpu_decoder_4x16_1_out_3[1]), .v(cpu_decoder_4x16_2_out_3[4]), .in_1(\input ),
    .\output (out_33), .s(set), .e(enable));
  CPU_REG_BYTE cpu_reg_byte_179 (
    .reset(reset), .h(cpu_decoder_4x16_1_out_3[2]), .v(cpu_decoder_4x16_2_out_3[4]), .in_1(\input ),
    .\output (out_49), .s(set), .e(enable));
  CPU_REG_BYTE cpu_reg_byte_180 (
    .reset(reset), .h(cpu_decoder_4x16_1_out_3[3]), .v(cpu_decoder_4x16_2_out_3[4]), .in_1(\input ),
    .\output (out_65), .s(set), .e(enable));
  CPU_REG_BYTE cpu_reg_byte_181 (
    .reset(reset), .h(cpu_decoder_4x16_1_out_3[4]), .v(cpu_decoder_4x16_2_out_3[4]), .in_1(\input ),
    .\output (out_81), .s(set), .e(enable));
  CPU_REG_BYTE cpu_reg_byte_182 (
    .reset(reset), .h(cpu_decoder_4x16_1_out_3[5]), .v(cpu_decoder_4x16_2_out_3[4]), .in_1(\input ),
    .\output (out_97), .s(set), .e(enable));
  CPU_REG_BYTE cpu_reg_byte_183 (
    .reset(reset), .h(cpu_decoder_4x16_1_out_3[6]), .v(cpu_decoder_4x16_2_out_3[4]), .in_1(\input ),
    .\output (out_113), .s(set), .e(enable));
  CPU_REG_BYTE cpu_reg_byte_184 (
    .reset(reset), .h(cpu_decoder_4x16_1_out_3[7]), .v(cpu_decoder_4x16_2_out_3[4]), .in_1(\input ),
    .\output (out_129), .s(set), .e(enable));
  CPU_REG_BYTE cpu_reg_byte_185 (
    .reset(reset), .h(cpu_decoder_4x16_1_out_3[8]), .v(cpu_decoder_4x16_2_out_3[4]), .in_1(\input ),
    .\output (out_145), .s(set), .e(enable));
  CPU_REG_BYTE cpu_reg_byte_186 (
    .reset(reset), .h(cpu_decoder_4x16_1_out_3[9]), .v(cpu_decoder_4x16_2_out_3[4]), .in_1(\input ),
    .\output (out_161), .s(set), .e(enable));
  CPU_REG_BYTE cpu_reg_byte_187 (
    .reset(reset), .h(cpu_decoder_4x16_1_out_3[10]), .v(cpu_decoder_4x16_2_out_3[4]), .in_1(\input ),
    .\output (out_177), .s(set), .e(enable));
  CPU_REG_BYTE cpu_reg_byte_188 (
    .reset(reset), .h(cpu_decoder_4x16_1_out_3[11]), .v(cpu_decoder_4x16_2_out_3[4]), .in_1(\input ),
    .\output (out_193), .s(set), .e(enable));
  CPU_REG_BYTE cpu_reg_byte_189 (
    .reset(reset), .h(cpu_decoder_4x16_1_out_3[12]), .v(cpu_decoder_4x16_2_out_3[4]), .in_1(\input ),
    .\output (out_209), .s(set), .e(enable));
  CPU_REG_BYTE cpu_reg_byte_190 (
    .reset(reset), .h(cpu_decoder_4x16_1_out_3[13]), .v(cpu_decoder_4x16_2_out_3[4]), .in_1(undriven),
    .\output (out_225), .s(set), .e(enable));
  CPU_REG_BYTE cpu_reg_byte_191 (
    .reset(reset), .h(cpu_decoder_4x16_1_out_3[14]), .v(cpu_decoder_4x16_2_out_3[4]), .in_1(undriven),
    .\output (out_241), .s(set), .e(enable));
  CPU_REG_BYTE cpu_reg_byte_192 (
    .reset(reset), .h(cpu_decoder_4x16_1_out_3[15]), .v(cpu_decoder_4x16_2_out_3[4]), .in_1(undriven),
    .\output (out_257), .s(set), .e(enable));
  CPU_REG_BYTE cpu_reg_byte_193 (
    .reset(reset), .h(cpu_decoder_4x16_1_out_3[0]), .v(cpu_decoder_4x16_2_out_3[3]), .in_1(\input ),
    .\output (out_18), .s(set), .e(enable));
  CPU_REG_BYTE cpu_reg_byte_194 (
    .reset(reset), .h(cpu_decoder_4x16_1_out_3[1]), .v(cpu_decoder_4x16_2_out_3[3]), .in_1(\input ),
    .\output (out_34), .s(set), .e(enable));
  CPU_REG_BYTE cpu_reg_byte_195 (
    .reset(reset), .h(cpu_decoder_4x16_1_out_3[2]), .v(cpu_decoder_4x16_2_out_3[3]), .in_1(\input ),
    .\output (out_50), .s(set), .e(enable));
  CPU_REG_BYTE cpu_reg_byte_196 (
    .reset(reset), .h(cpu_decoder_4x16_1_out_3[3]), .v(cpu_decoder_4x16_2_out_3[3]), .in_1(\input ),
    .\output (out_66), .s(set), .e(enable));
  CPU_REG_BYTE cpu_reg_byte_197 (
    .reset(reset), .h(cpu_decoder_4x16_1_out_3[4]), .v(cpu_decoder_4x16_2_out_3[3]), .in_1(\input ),
    .\output (out_82), .s(set), .e(enable));
  CPU_REG_BYTE cpu_reg_byte_198 (
    .reset(reset), .h(cpu_decoder_4x16_1_out_3[5]), .v(cpu_decoder_4x16_2_out_3[3]), .in_1(\input ),
    .\output (out_98), .s(set), .e(enable));
  CPU_REG_BYTE cpu_reg_byte_199 (
    .reset(reset), .h(cpu_decoder_4x16_1_out_3[6]), .v(cpu_decoder_4x16_2_out_3[3]), .in_1(\input ),
    .\output (out_114), .s(set), .e(enable));
  CPU_REG_BYTE cpu_reg_byte_200 (
    .reset(reset), .h(cpu_decoder_4x16_1_out_3[7]), .v(cpu_decoder_4x16_2_out_3[3]), .in_1(\input ),
    .\output (out_130), .s(set), .e(enable));
  CPU_REG_BYTE cpu_reg_byte_201 (
    .reset(reset), .h(cpu_decoder_4x16_1_out_3[8]), .v(cpu_decoder_4x16_2_out_3[3]), .in_1(\input ),
    .\output (out_146), .s(set), .e(enable));
  CPU_REG_BYTE cpu_reg_byte_202 (
    .reset(reset), .h(cpu_decoder_4x16_1_out_3[9]), .v(cpu_decoder_4x16_2_out_3[3]), .in_1(\input ),
    .\output (out_162), .s(set), .e(enable));
  CPU_REG_BYTE cpu_reg_byte_203 (
    .reset(reset), .h(cpu_decoder_4x16_1_out_3[10]), .v(cpu_decoder_4x16_2_out_3[3]), .in_1(\input ),
    .\output (out_178), .s(set), .e(enable));
  CPU_REG_BYTE cpu_reg_byte_204 (
    .reset(reset), .h(cpu_decoder_4x16_1_out_3[11]), .v(cpu_decoder_4x16_2_out_3[3]), .in_1(\input ),
    .\output (out_194), .s(set), .e(enable));
  CPU_REG_BYTE cpu_reg_byte_205 (
    .reset(reset), .h(cpu_decoder_4x16_1_out_3[12]), .v(cpu_decoder_4x16_2_out_3[3]), .in_1(\input ),
    .\output (out_210), .s(set), .e(enable));
  CPU_REG_BYTE cpu_reg_byte_206 (
    .reset(reset), .h(cpu_decoder_4x16_1_out_3[13]), .v(cpu_decoder_4x16_2_out_3[3]), .in_1(undriven),
    .\output (out_226), .s(set), .e(enable));
  CPU_REG_BYTE cpu_reg_byte_207 (
    .reset(reset), .h(cpu_decoder_4x16_1_out_3[14]), .v(cpu_decoder_4x16_2_out_3[3]), .in_1(undriven),
    .\output (out_242), .s(set), .e(enable));
  CPU_REG_BYTE cpu_reg_byte_208 (
    .reset(reset), .h(cpu_decoder_4x16_1_out_3[15]), .v(cpu_decoder_4x16_2_out_3[3]), .in_1(undriven),
    .\output (out_258), .s(set), .e(enable));
  CPU_REG_BYTE cpu_reg_byte_209 (
    .reset(reset), .h(cpu_decoder_4x16_1_out_3[0]), .v(cpu_decoder_4x16_2_out_3[2]), .in_1(\input ),
    .\output (out_19), .s(set), .e(enable));
  CPU_REG_BYTE cpu_reg_byte_210 (
    .reset(reset), .h(cpu_decoder_4x16_1_out_3[1]), .v(cpu_decoder_4x16_2_out_3[2]), .in_1(\input ),
    .\output (out_35), .s(set), .e(enable));
  CPU_REG_BYTE cpu_reg_byte_211 (
    .reset(reset), .h(cpu_decoder_4x16_1_out_3[2]), .v(cpu_decoder_4x16_2_out_3[2]), .in_1(\input ),
    .\output (out_51), .s(set), .e(enable));
  CPU_REG_BYTE cpu_reg_byte_212 (
    .reset(reset), .h(cpu_decoder_4x16_1_out_3[3]), .v(cpu_decoder_4x16_2_out_3[2]), .in_1(\input ),
    .\output (out_67), .s(set), .e(enable));
  CPU_REG_BYTE cpu_reg_byte_213 (
    .reset(reset), .h(cpu_decoder_4x16_1_out_3[4]), .v(cpu_decoder_4x16_2_out_3[2]), .in_1(\input ),
    .\output (out_83), .s(set), .e(enable));
  CPU_REG_BYTE cpu_reg_byte_214 (
    .reset(reset), .h(cpu_decoder_4x16_1_out_3[5]), .v(cpu_decoder_4x16_2_out_3[2]), .in_1(\input ),
    .\output (out_99), .s(set), .e(enable));
  CPU_REG_BYTE cpu_reg_byte_215 (
    .reset(reset), .h(cpu_decoder_4x16_1_out_3[6]), .v(cpu_decoder_4x16_2_out_3[2]), .in_1(\input ),
    .\output (out_115), .s(set), .e(enable));
  CPU_REG_BYTE cpu_reg_byte_216 (
    .reset(reset), .h(cpu_decoder_4x16_1_out_3[7]), .v(cpu_decoder_4x16_2_out_3[2]), .in_1(\input ),
    .\output (out_131), .s(set), .e(enable));
  CPU_REG_BYTE cpu_reg_byte_217 (
    .reset(reset), .h(cpu_decoder_4x16_1_out_3[8]), .v(cpu_decoder_4x16_2_out_3[2]), .in_1(\input ),
    .\output (out_147), .s(set), .e(enable));
  CPU_REG_BYTE cpu_reg_byte_218 (
    .reset(reset), .h(cpu_decoder_4x16_1_out_3[9]), .v(cpu_decoder_4x16_2_out_3[2]), .in_1(\input ),
    .\output (out_163), .s(set), .e(enable));
  CPU_REG_BYTE cpu_reg_byte_219 (
    .reset(reset), .h(cpu_decoder_4x16_1_out_3[10]), .v(cpu_decoder_4x16_2_out_3[2]), .in_1(\input ),
    .\output (out_179), .s(set), .e(enable));
  CPU_REG_BYTE cpu_reg_byte_220 (
    .reset(reset), .h(cpu_decoder_4x16_1_out_3[11]), .v(cpu_decoder_4x16_2_out_3[2]), .in_1(\input ),
    .\output (out_195), .s(set), .e(enable));
  CPU_REG_BYTE cpu_reg_byte_221 (
    .reset(reset), .h(cpu_decoder_4x16_1_out_3[12]), .v(cpu_decoder_4x16_2_out_3[2]), .in_1(\input ),
    .\output (out_211), .s(set), .e(enable));
  CPU_REG_BYTE cpu_reg_byte_222 (
    .reset(reset), .h(cpu_decoder_4x16_1_out_3[13]), .v(cpu_decoder_4x16_2_out_3[2]), .in_1(undriven),
    .\output (out_227), .s(set), .e(enable));
  CPU_REG_BYTE cpu_reg_byte_223 (
    .reset(reset), .h(cpu_decoder_4x16_1_out_3[14]), .v(cpu_decoder_4x16_2_out_3[2]), .in_1(undriven),
    .\output (out_243), .s(set), .e(enable));
  CPU_REG_BYTE cpu_reg_byte_224 (
    .reset(reset), .h(cpu_decoder_4x16_1_out_3[15]), .v(cpu_decoder_4x16_2_out_3[2]), .in_1(undriven),
    .\output (out_259), .s(set), .e(enable));
  CPU_REG_BYTE cpu_reg_byte_225 (
    .reset(reset), .h(cpu_decoder_4x16_1_out_3[0]), .v(cpu_decoder_4x16_2_out_3[1]), .in_1(\input ),
    .\output (out_20), .s(set), .e(enable));
  CPU_REG_BYTE cpu_reg_byte_226 (
    .h(cpu_decoder_4x16_1_out_3[1]), .v(cpu_decoder_4x16_2_out_3[1]), .in_1(\input ), .\output (out_36),
    .s(set), .e(enable));  // open: reset
  CPU_REG_BYTE cpu_reg_byte_227 (
    .reset(reset), .h(cpu_decoder_4x16_1_out_3[2]), .v(cpu_decoder_4x16_2_out_3[1]), .in_1(\input ),
    .\output (out_52), .s(set), .e(enable));
  CPU_REG_BYTE cpu_reg_byte_228 (
    .reset(reset), .h(cpu_decoder_4x16_1_out_3[3]), .v(cpu_decoder_4x16_2_out_3[1]), .in_1(\input ),
    .\output (out_68), .s(set), .e(enable));
  CPU_REG_BYTE cpu_reg_byte_229 (
    .reset(reset), .h(cpu_decoder_4x16_1_out_3[4]), .v(cpu_decoder_4x16_2_out_3[1]), .in_1(\input ),
    .\output (out_84), .s(set), .e(enable));
  CPU_REG_BYTE cpu_reg_byte_230 (
    .reset(reset), .h(cpu_decoder_4x16_1_out_3[5]), .v(cpu_decoder_4x16_2_out_3[1]), .in_1(\input ),
    .\output (out_100), .s(set), .e(enable));
  CPU_REG_BYTE cpu_reg_byte_231 (
    .reset(reset), .h(cpu_decoder_4x16_1_out_3[6]), .v(cpu_decoder_4x16_2_out_3[1]), .in_1(\input ),
    .\output (out_116), .s(set), .e(enable));
  CPU_REG_BYTE cpu_reg_byte_232 (
    .reset(reset), .h(cpu_decoder_4x16_1_out_3[7]), .v(cpu_decoder_4x16_2_out_3[1]), .in_1(\input ),
    .\output (out_132), .s(set), .e(enable));
  CPU_REG_BYTE cpu_reg_byte_233 (
    .reset(reset), .h(cpu_decoder_4x16_1_out_3[8]), .v(cpu_decoder_4x16_2_out_3[1]), .in_1(\input ),
    .\output (out_148), .s(set), .e(enable));
  CPU_REG_BYTE cpu_reg_byte_234 (
    .reset(reset), .h(cpu_decoder_4x16_1_out_3[9]), .v(cpu_decoder_4x16_2_out_3[1]), .in_1(\input ),
    .\output (out_164), .s(set), .e(enable));
  CPU_REG_BYTE cpu_reg_byte_235 (
    .reset(reset), .h(cpu_decoder_4x16_1_out_3[10]), .v(cpu_decoder_4x16_2_out_3[1]), .in_1(\input ),
    .\output (out_180), .s(set), .e(enable));
  CPU_REG_BYTE cpu_reg_byte_236 (
    .reset(reset), .h(cpu_decoder_4x16_1_out_3[11]), .v(cpu_decoder_4x16_2_out_3[1]), .in_1(\input ),
    .\output (out_196), .s(set), .e(enable));
  CPU_REG_BYTE cpu_reg_byte_237 (
    .reset(reset), .h(cpu_decoder_4x16_1_out_3[12]), .v(cpu_decoder_4x16_2_out_3[1]), .in_1(\input ),
    .\output (out_212), .s(set), .e(enable));
  CPU_REG_BYTE cpu_reg_byte_238 (
    .reset(reset), .h(cpu_decoder_4x16_1_out_3[13]), .v(cpu_decoder_4x16_2_out_3[1]), .in_1(undriven),
    .\output (out_228), .s(set), .e(enable));
  CPU_REG_BYTE cpu_reg_byte_239 (
    .reset(reset), .h(cpu_decoder_4x16_1_out_3[14]), .v(cpu_decoder_4x16_2_out_3[1]), .in_1(undriven),
    .\output (out_244), .s(set), .e(enable));
  CPU_REG_BYTE cpu_reg_byte_240 (
    .reset(reset), .h(cpu_decoder_4x16_1_out_3[15]), .v(cpu_decoder_4x16_2_out_3[1]), .in_1(undriven),
    .\output (out_260), .s(set), .e(enable));
  CPU_REG_BYTE cpu_reg_byte_241 (
    .reset(reset), .h(cpu_decoder_4x16_1_out_3[0]), .v(cpu_decoder_4x16_2_out_3[0]), .in_1(\input ),
    .\output (out_21), .s(set), .e(enable));
  CPU_REG_BYTE cpu_reg_byte_242 (
    .reset(reset), .h(cpu_decoder_4x16_1_out_3[1]), .v(cpu_decoder_4x16_2_out_3[0]), .in_1(\input ),
    .\output (out_37), .s(set), .e(enable));
  CPU_REG_BYTE cpu_reg_byte_243 (
    .reset(reset), .h(cpu_decoder_4x16_1_out_3[2]), .v(cpu_decoder_4x16_2_out_3[0]), .in_1(\input ),
    .\output (out_53), .s(set), .e(enable));
  CPU_REG_BYTE cpu_reg_byte_244 (
    .reset(reset), .h(cpu_decoder_4x16_1_out_3[3]), .v(cpu_decoder_4x16_2_out_3[0]), .in_1(\input ),
    .\output (out_69), .s(set), .e(enable));
  CPU_REG_BYTE cpu_reg_byte_245 (
    .reset(reset), .h(cpu_decoder_4x16_1_out_3[4]), .v(cpu_decoder_4x16_2_out_3[0]), .in_1(\input ),
    .\output (out_85), .s(set), .e(enable));
  CPU_REG_BYTE cpu_reg_byte_246 (
    .reset(reset), .h(cpu_decoder_4x16_1_out_3[5]), .v(cpu_decoder_4x16_2_out_3[0]), .in_1(\input ),
    .\output (out_101), .s(set), .e(enable));
  CPU_REG_BYTE cpu_reg_byte_247 (
    .reset(reset), .h(cpu_decoder_4x16_1_out_3[6]), .v(cpu_decoder_4x16_2_out_3[0]), .in_1(\input ),
    .\output (out_117), .s(set), .e(enable));
  CPU_REG_BYTE cpu_reg_byte_248 (
    .reset(reset), .h(cpu_decoder_4x16_1_out_3[7]), .v(cpu_decoder_4x16_2_out_3[0]), .in_1(\input ),
    .\output (out_133), .s(set), .e(enable));
  CPU_REG_BYTE cpu_reg_byte_249 (
    .reset(reset), .h(cpu_decoder_4x16_1_out_3[8]), .v(cpu_decoder_4x16_2_out_3[0]), .in_1(\input ),
    .\output (out_149), .s(set), .e(enable));
  CPU_REG_BYTE cpu_reg_byte_250 (
    .reset(reset), .h(cpu_decoder_4x16_1_out_3[9]), .v(cpu_decoder_4x16_2_out_3[0]), .in_1(\input ),
    .\output (out_165), .s(set), .e(enable));
  CPU_REG_BYTE cpu_reg_byte_251 (
    .reset(reset), .h(cpu_decoder_4x16_1_out_3[10]), .v(cpu_decoder_4x16_2_out_3[0]), .in_1(\input ),
    .\output (out_181), .s(set), .e(enable));
  CPU_REG_BYTE cpu_reg_byte_252 (
    .reset(reset), .h(cpu_decoder_4x16_1_out_3[11]), .v(cpu_decoder_4x16_2_out_3[0]), .in_1(\input ),
    .\output (out_197), .s(set), .e(enable));
  CPU_REG_BYTE cpu_reg_byte_253 (
    .reset(reset), .h(cpu_decoder_4x16_1_out_3[12]), .v(cpu_decoder_4x16_2_out_3[0]), .in_1(\input ),
    .\output (out_213), .s(set), .e(enable));
  CPU_REG_BYTE cpu_reg_byte_254 (
    .reset(reset), .h(cpu_decoder_4x16_1_out_3[13]), .v(cpu_decoder_4x16_2_out_3[0]), .in_1(undriven),
    .\output (out_229), .s(set), .e(enable));
  CPU_REG_BYTE cpu_reg_byte_255 (
    .reset(reset), .h(cpu_decoder_4x16_1_out_3[14]), .v(cpu_decoder_4x16_2_out_3[0]), .in_1(undriven),
    .\output (out_245), .s(set), .e(enable));
  CPU_REG_BYTE cpu_reg_byte_256 (
    .reset(reset), .h(cpu_decoder_4x16_1_out_3[15]), .v(cpu_decoder_4x16_2_out_3[0]), .in_1(undriven),
    .\output (out_261), .s(set), .e(enable));
endmodule

module CPU_MEM_1 (
  input  s,
  input  e,
  output e_2
);

  wire nand_1_out, nand_2_out, nand_4_out;

  nand nand_1 (nand_1_out, s, e);
  nand nand_2 (nand_2_out, nand_1_out, e);
  nand nand_3 (e_2, nand_1_out, nand_4_out);
  nand nand_4 (nand_4_out, e_2, nand_2_out);
endmodule
