// Logisim project LOAD+AND+STORE+INSTRUCTIONS.circ as structural Verilog
module CPU_MEM_1 (
  input  in_1,
  input  in_2,
  output out_3
);

  wire nand_1_out, nand_2_out, nand_4_out;

  nand nand_1 (nand_1_out, in_1, in_2);
  nand nand_2 (nand_2_out, nand_1_out, in_2);
  nand nand_3 (out_3, nand_1_out, nand_4_out);
  nand nand_4 (nand_4_out, out_3, nand_2_out);

  // Notes on the sheet:
  //   in_2: pull=down
  //   in_1: pull=down
  //   out_3: pull=down
endmodule

module CPU_MEM_8 (
  input  [7:0] in_1,
  input  s,
  output [7:0] out_3
);

  CPU_MEM_1 cpu_mem_1_1 (.in_1(in_1[0]), .in_2(s), .out_3(out_3[0]));
  CPU_MEM_1 cpu_mem_1_2 (.in_1(in_1[1]), .in_2(s), .out_3(out_3[1]));
  CPU_MEM_1 cpu_mem_1_3 (.in_1(in_1[2]), .in_2(s), .out_3(out_3[2]));
  CPU_MEM_1 cpu_mem_1_4 (.in_1(in_1[3]), .in_2(s), .out_3(out_3[3]));
  CPU_MEM_1 cpu_mem_1_5 (.in_1(in_1[4]), .in_2(s), .out_3(out_3[4]));
  CPU_MEM_1 cpu_mem_1_6 (.in_1(in_1[5]), .in_2(s), .out_3(out_3[5]));
  CPU_MEM_1 cpu_mem_1_7 (.in_1(in_1[6]), .in_2(s), .out_3(out_3[6]));
  CPU_MEM_1 cpu_mem_1_8 (.in_1(in_1[7]), .in_2(s), .out_3(out_3[7]));

  // Notes on the sheet:
  //   out_3: pull=down
  //   in_1: pull=down
  //   s: pull=down
endmodule

module CPU_ENABLE_8 (
  input  [7:0] in_1,
  input  in_2,
  output [7:0] out_3
);

  wire and_1_out, and_2_out, and_3_out, and_4_out, and_5_out, and_6_out, and_7_out, and_8_out;

  and and_1 (and_1_out, in_1[0], in_2);
  assign out_3[0] = in_2 ? and_1_out : 1'bz;  // Controlled_Buffer controlled_buffer_1
  assign out_3[1] = in_2 ? and_2_out : 1'bz;  // Controlled_Buffer controlled_buffer_2
  and and_2 (and_2_out, in_1[1], in_2);
  and and_3 (and_3_out, in_1[2], in_2);
  assign out_3[2] = in_2 ? and_3_out : 1'bz;  // Controlled_Buffer controlled_buffer_3
  assign out_3[3] = in_2 ? and_4_out : 1'bz;  // Controlled_Buffer controlled_buffer_4
  and and_4 (and_4_out, in_1[3], in_2);
  assign out_3[4] = in_2 ? and_5_out : 1'bz;  // Controlled_Buffer controlled_buffer_5
  and and_5 (and_5_out, in_1[4], in_2);
  and and_6 (and_6_out, in_1[5], in_2);
  assign out_3[5] = in_2 ? and_6_out : 1'bz;  // Controlled_Buffer controlled_buffer_6
  and and_7 (and_7_out, in_1[6], in_2);
  assign out_3[6] = in_2 ? and_7_out : 1'bz;  // Controlled_Buffer controlled_buffer_7
  assign out_3[7] = in_2 ? and_8_out : 1'bz;  // Controlled_Buffer controlled_buffer_8
  and and_8 (and_8_out, in_1[7], in_2);
endmodule

module CPU_REGISTER_8 (
  input  [7:0] i,
  input  s,
  input  e,
  output [7:0] _0
);

  wire [7:0] cpu_enable_8_1_out_3, cpu_mem_8_1_out_3;

  CPU_MEM_8 cpu_mem_8_1 (.s(s), .in_1(i), .out_3(cpu_mem_8_1_out_3));
  CPU_ENABLE_8 cpu_enable_8_1 (.in_1(cpu_mem_8_1_out_3), .out_3(cpu_enable_8_1_out_3), .in_2(e));
  assign _0 = e ? cpu_enable_8_1_out_3 : 8'bz;  // Controlled_Buffer controlled_buffer_1

  // Notes on the sheet:
  //   e: pull=down
  //   i: pull=down
  //   _0: pull=down
  //   s: pull=down
endmodule

module CPU_DECODER_4x16 (
  input  [3:0] in_1,
  output L,
  output out_3,
  output out_4,
  output out_5,
  output out_6,
  output out_7,
  output out_8,
  output out_9,
  output out_10,
  output out_11,
  output out_12,
  output out_13,
  output out_14,
  output out_15,
  output out_16,
  output M
);

  wire not_1_out, not_2_out, not_3_out, not_4_out;

  not not_1 (not_1_out, in_1[0]);
  not not_2 (not_2_out, in_1[1]);
  not not_3 (not_3_out, in_1[2]);
  not not_4 (not_4_out, in_1[3]);
  and and_1 (L, not_4_out, not_3_out, not_2_out, not_1_out);
  and and_2 (out_3, not_4_out, not_3_out, not_2_out, in_1[0]);
  and and_3 (out_4, not_4_out, not_3_out, in_1[1], not_1_out);
  and and_4 (out_5, not_4_out, not_3_out, in_1[1], in_1[0]);
  and and_5 (out_6, not_4_out, in_1[2], not_2_out, not_1_out);
  and and_6 (out_7, not_4_out, in_1[2], not_2_out, in_1[0]);
  and and_7 (out_8, not_4_out, in_1[2], in_1[1], not_1_out);
  and and_8 (out_9, not_4_out, in_1[2], in_1[1], in_1[0]);
  and and_9 (out_10, in_1[3], not_3_out, not_2_out, not_1_out);
  and and_10 (out_11, in_1[3], not_3_out, not_2_out, in_1[0]);
  and and_11 (out_12, in_1[3], not_3_out, in_1[1], not_1_out);
  and and_12 (out_13, in_1[3], not_3_out, in_1[1], in_1[0]);
  and and_13 (out_14, in_1[3], in_1[2], not_2_out, not_1_out);
  and and_14 (out_15, in_1[3], in_1[2], not_2_out, in_1[0]);
  and and_15 (out_16, in_1[3], in_1[2], in_1[1], not_1_out);
  and and_16 (M, in_1[3], in_1[2], in_1[1], in_1[0]);

  // Notes on the sheet:
  //   in_1: pull=down
  //   out_13: pull=down
  //   out_9: pull=down
  //   out_16: pull=down
  //   M: pull=down
  //   out_6: pull=down
  //   out_15: pull=down
  //   out_7: pull=down
  //   L: pull=down
  //   out_14: pull=down
  //   out_3: pull=down
  //   out_12: pull=down
  //   out_10: pull=down
  //   out_8: pull=down
  //   out_5: pull=down
  //   out_4: pull=down
  //   out_11: pull=down
endmodule

module CPU_REG_BYTE (
  input  [7:0] i,
  input  h,
  input  v,
  input  s,
  input  e,
  output [7:0] o
);

  wire and_1_out, and_2_out, and_3_out;
  wire [7:0] cpu_register_8_1__0;

  and and_1 (and_1_out, h, v);
  and and_2 (and_2_out, and_1_out, s);
  and and_3 (and_3_out, and_1_out, e);
  CPU_REGISTER_8 cpu_register_8_1 (.i(i), .s(and_2_out), .e(and_3_out), ._0(cpu_register_8_1__0));
  assign o = and_3_out ? cpu_register_8_1__0 : 8'bz;  // Controlled_Buffer controlled_buffer_1

  // Notes on the sheet:
  //   i: pull=down
  //   s: pull=down
  //   h: pull=down
  //   e: pull=down
  //   o: pull=down
  //   v: pull=down
endmodule

module CPU_RAM_256 (
  input  [7:0] i,
  input  sa,
  input  [7:0] address,
  input  s,
  input  e,
  output [7:0] o
);

  wire cpu_decoder_4x16_1_l, cpu_decoder_4x16_1_m, cpu_decoder_4x16_1_out_3, cpu_decoder_4x16_1_out_4,
       cpu_decoder_4x16_1_out_5, cpu_decoder_4x16_1_out_6, cpu_decoder_4x16_1_out_7,
       cpu_decoder_4x16_1_out_8, cpu_decoder_4x16_1_out_9, cpu_decoder_4x16_1_out_10,
       cpu_decoder_4x16_1_out_11, cpu_decoder_4x16_1_out_12, cpu_decoder_4x16_1_out_13,
       cpu_decoder_4x16_1_out_14, cpu_decoder_4x16_1_out_15, cpu_decoder_4x16_1_out_16, cpu_decoder_4x16_2_l,
       cpu_decoder_4x16_2_m, cpu_decoder_4x16_2_out_3, cpu_decoder_4x16_2_out_4, cpu_decoder_4x16_2_out_5,
       cpu_decoder_4x16_2_out_6, cpu_decoder_4x16_2_out_7, cpu_decoder_4x16_2_out_8,
       cpu_decoder_4x16_2_out_9, cpu_decoder_4x16_2_out_10, cpu_decoder_4x16_2_out_11,
       cpu_decoder_4x16_2_out_12, cpu_decoder_4x16_2_out_13, cpu_decoder_4x16_2_out_14,
       cpu_decoder_4x16_2_out_15, cpu_decoder_4x16_2_out_16;
  wire [7:0] cpu_mem_8_1_out_3, cpu_reg_byte_1_o;

  CPU_MEM_8 cpu_mem_8_1 (.s(sa), .in_1(address), .out_3(cpu_mem_8_1_out_3));
  CPU_DECODER_4x16 cpu_decoder_4x16_1 (
    .in_1(cpu_mem_8_1_out_3[7:4]), .L(cpu_decoder_4x16_1_l), .out_3(cpu_decoder_4x16_1_out_3),
    .out_4(cpu_decoder_4x16_1_out_4), .out_5(cpu_decoder_4x16_1_out_5), .out_6(cpu_decoder_4x16_1_out_6),
    .out_7(cpu_decoder_4x16_1_out_7), .out_8(cpu_decoder_4x16_1_out_8), .out_9(cpu_decoder_4x16_1_out_9),
    .out_10(cpu_decoder_4x16_1_out_10), .out_11(cpu_decoder_4x16_1_out_11),
    .out_12(cpu_decoder_4x16_1_out_12), .out_13(cpu_decoder_4x16_1_out_13),
    .out_14(cpu_decoder_4x16_1_out_14), .out_15(cpu_decoder_4x16_1_out_15),
    .out_16(cpu_decoder_4x16_1_out_16), .M(cpu_decoder_4x16_1_m));
  assign o = e ? cpu_reg_byte_1_o : 8'bz;  // Controlled_Buffer controlled_buffer_1
  CPU_REG_BYTE cpu_reg_byte_1 (
    .h(cpu_decoder_4x16_1_l), .v(cpu_decoder_4x16_2_m), .i(i), .o(cpu_reg_byte_1_o), .s(s), .e(e));
  CPU_REG_BYTE cpu_reg_byte_2 (
    .h(cpu_decoder_4x16_1_out_3), .v(cpu_decoder_4x16_2_m), .i(i), .o(cpu_reg_byte_1_o), .s(s), .e(e));
  CPU_REG_BYTE cpu_reg_byte_3 (
    .h(cpu_decoder_4x16_1_l), .v(cpu_decoder_4x16_2_out_16), .i(i), .o(cpu_reg_byte_1_o), .s(s), .e(e));
  CPU_REG_BYTE cpu_reg_byte_4 (
    .h(cpu_decoder_4x16_1_out_3), .v(cpu_decoder_4x16_2_out_16), .i(i), .o(cpu_reg_byte_1_o), .s(s), .e(e));
  CPU_REG_BYTE cpu_reg_byte_5 (
    .h(cpu_decoder_4x16_1_l), .v(cpu_decoder_4x16_2_out_15), .i(i), .o(cpu_reg_byte_1_o), .s(s), .e(e));
  CPU_REG_BYTE cpu_reg_byte_6 (
    .h(cpu_decoder_4x16_1_out_3), .v(cpu_decoder_4x16_2_out_15), .i(i), .o(cpu_reg_byte_1_o), .s(s), .e(e));
  CPU_REG_BYTE cpu_reg_byte_7 (
    .h(cpu_decoder_4x16_1_l), .v(cpu_decoder_4x16_2_out_14), .i(i), .o(cpu_reg_byte_1_o), .s(s), .e(e));
  CPU_REG_BYTE cpu_reg_byte_8 (
    .h(cpu_decoder_4x16_1_out_3), .v(cpu_decoder_4x16_2_out_14), .i(i), .o(cpu_reg_byte_1_o), .s(s), .e(e));
  CPU_REG_BYTE cpu_reg_byte_9 (
    .h(cpu_decoder_4x16_1_l), .v(cpu_decoder_4x16_2_out_13), .i(i), .o(cpu_reg_byte_1_o), .s(s), .e(e));
  CPU_REG_BYTE cpu_reg_byte_10 (
    .h(cpu_decoder_4x16_1_out_3), .v(cpu_decoder_4x16_2_out_13), .i(i), .o(cpu_reg_byte_1_o), .s(s), .e(e));
  CPU_REG_BYTE cpu_reg_byte_11 (
    .h(cpu_decoder_4x16_1_l), .v(cpu_decoder_4x16_2_out_12), .i(i), .o(cpu_reg_byte_1_o), .s(s), .e(e));
  CPU_REG_BYTE cpu_reg_byte_12 (
    .h(cpu_decoder_4x16_1_out_3), .v(cpu_decoder_4x16_2_out_12), .i(i), .o(cpu_reg_byte_1_o), .s(s), .e(e));
  CPU_REG_BYTE cpu_reg_byte_13 (
    .h(cpu_decoder_4x16_1_l), .v(cpu_decoder_4x16_2_out_11), .i(i), .o(cpu_reg_byte_1_o), .s(s), .e(e));
  CPU_REG_BYTE cpu_reg_byte_14 (
    .h(cpu_decoder_4x16_1_out_3), .v(cpu_decoder_4x16_2_out_11), .i(i), .o(cpu_reg_byte_1_o), .s(s), .e(e));
  CPU_REG_BYTE cpu_reg_byte_15 (
    .h(cpu_decoder_4x16_1_l), .v(cpu_decoder_4x16_2_out_10), .i(i), .o(cpu_reg_byte_1_o), .s(s), .e(e));
  CPU_REG_BYTE cpu_reg_byte_16 (
    .h(cpu_decoder_4x16_1_out_3), .v(cpu_decoder_4x16_2_out_10), .i(i), .o(cpu_reg_byte_1_o), .s(s), .e(e));
  CPU_DECODER_4x16 cpu_decoder_4x16_2 (
    .in_1(cpu_mem_8_1_out_3[3:0]), .L(cpu_decoder_4x16_2_l), .out_3(cpu_decoder_4x16_2_out_3),
    .out_4(cpu_decoder_4x16_2_out_4), .out_5(cpu_decoder_4x16_2_out_5), .out_6(cpu_decoder_4x16_2_out_6),
    .out_7(cpu_decoder_4x16_2_out_7), .out_8(cpu_decoder_4x16_2_out_8), .out_9(cpu_decoder_4x16_2_out_9),
    .out_10(cpu_decoder_4x16_2_out_10), .out_11(cpu_decoder_4x16_2_out_11),
    .out_12(cpu_decoder_4x16_2_out_12), .out_13(cpu_decoder_4x16_2_out_13),
    .out_14(cpu_decoder_4x16_2_out_14), .out_15(cpu_decoder_4x16_2_out_15),
    .out_16(cpu_decoder_4x16_2_out_16), .M(cpu_decoder_4x16_2_m));
  CPU_REG_BYTE cpu_reg_byte_17 (
    .h(cpu_decoder_4x16_1_l), .v(cpu_decoder_4x16_2_out_9), .i(i), .o(cpu_reg_byte_1_o), .s(s), .e(e));
  CPU_REG_BYTE cpu_reg_byte_18 (
    .h(cpu_decoder_4x16_1_out_3), .v(cpu_decoder_4x16_2_out_9), .i(i), .o(cpu_reg_byte_1_o), .s(s), .e(e));
  CPU_REG_BYTE cpu_reg_byte_19 (
    .h(cpu_decoder_4x16_1_l), .v(cpu_decoder_4x16_2_out_8), .i(i), .o(cpu_reg_byte_1_o), .s(s), .e(e));
  CPU_REG_BYTE cpu_reg_byte_20 (
    .h(cpu_decoder_4x16_1_out_3), .v(cpu_decoder_4x16_2_out_8), .i(i), .o(cpu_reg_byte_1_o), .s(s), .e(e));
  CPU_REG_BYTE cpu_reg_byte_21 (
    .h(cpu_decoder_4x16_1_l), .v(cpu_decoder_4x16_2_out_7), .i(i), .o(cpu_reg_byte_1_o), .s(s), .e(e));
  CPU_REG_BYTE cpu_reg_byte_22 (
    .h(cpu_decoder_4x16_1_out_3), .v(cpu_decoder_4x16_2_out_7), .i(i), .o(cpu_reg_byte_1_o), .s(s), .e(e));
  CPU_REG_BYTE cpu_reg_byte_23 (
    .h(cpu_decoder_4x16_1_l), .v(cpu_decoder_4x16_2_out_6), .i(i), .o(cpu_reg_byte_1_o), .s(s), .e(e));
  CPU_REG_BYTE cpu_reg_byte_24 (
    .h(cpu_decoder_4x16_1_out_3), .v(cpu_decoder_4x16_2_out_6), .i(i), .o(cpu_reg_byte_1_o), .s(s), .e(e));
  CPU_REG_BYTE cpu_reg_byte_25 (
    .h(cpu_decoder_4x16_1_l), .v(cpu_decoder_4x16_2_out_5), .i(i), .o(cpu_reg_byte_1_o), .s(s), .e(e));
  CPU_REG_BYTE cpu_reg_byte_26 (
    .h(cpu_decoder_4x16_1_out_3), .v(cpu_decoder_4x16_2_out_5), .i(i), .o(cpu_reg_byte_1_o), .s(s), .e(e));
  CPU_REG_BYTE cpu_reg_byte_27 (
    .h(cpu_decoder_4x16_1_l), .v(cpu_decoder_4x16_2_out_4), .i(i), .o(cpu_reg_byte_1_o), .s(s), .e(e));
  CPU_REG_BYTE cpu_reg_byte_28 (
    .h(cpu_decoder_4x16_1_out_3), .v(cpu_decoder_4x16_2_out_4), .i(i), .o(cpu_reg_byte_1_o), .s(s), .e(e));
  CPU_REG_BYTE cpu_reg_byte_29 (
    .h(cpu_decoder_4x16_1_l), .v(cpu_decoder_4x16_2_out_3), .i(i), .o(cpu_reg_byte_1_o), .s(s), .e(e));
  CPU_REG_BYTE cpu_reg_byte_30 (
    .h(cpu_decoder_4x16_1_out_3), .v(cpu_decoder_4x16_2_out_3), .i(i), .o(cpu_reg_byte_1_o), .s(s), .e(e));
  CPU_REG_BYTE cpu_reg_byte_31 (
    .h(cpu_decoder_4x16_1_l), .v(cpu_decoder_4x16_2_l), .i(i), .o(cpu_reg_byte_1_o), .s(s), .e(e));
  CPU_REG_BYTE cpu_reg_byte_32 (
    .h(cpu_decoder_4x16_1_out_3), .v(cpu_decoder_4x16_2_l), .i(i), .o(cpu_reg_byte_1_o), .s(s), .e(e));

  // Notes on the sheet:
  //   address: pull=down
  //   i: pull=down
  //   o: pull=down
  //   sa: pull=down
endmodule

module CPU_NOT (
  input  [7:0] i,
  output [7:0] out_2
);

  not not_1 (out_2[0], i[0]);
  not not_2 (out_2[1], i[1]);
  not not_3 (out_2[2], i[2]);
  not not_4 (out_2[3], i[3]);
  not not_5 (out_2[4], i[4]);
  not not_6 (out_2[5], i[5]);
  not not_7 (out_2[6], i[6]);
  not not_8 (out_2[7], i[7]);
endmodule

module CPU_AND (
  input  [7:0] a,
  input  [7:0] b,
  output [7:0] o
);

  and and_1 (o[0], a[0], b[0]);
  and and_2 (o[1], a[1], b[1]);
  and and_3 (o[2], a[2], b[2]);
  and and_4 (o[3], a[3], b[3]);
  and and_5 (o[4], a[4], b[4]);
  and and_6 (o[5], a[5], b[5]);
  and and_7 (o[6], a[6], b[6]);
  and and_8 (o[7], a[7], b[7]);
endmodule

module CPU_OR (
  input  [7:0] a,
  input  [7:0] b,
  output [7:0] _0
);

  or or_1 (_0[0], a[0], b[0]);
  or or_2 (_0[1], a[1], b[1]);
  or or_3 (_0[2], a[2], b[2]);
  or or_4 (_0[3], a[3], b[3]);
  or or_5 (_0[4], a[4], b[4]);
  or or_6 (_0[5], a[5], b[5]);
  or or_7 (_0[6], a[6], b[6]);
  or or_8 (_0[7], a[7], b[7]);
endmodule

module CPU_XOR_1 (
  input  a,
  input  b,
  output o
);

  wire nand_1_out, nand_2_out, not_1_out, not_2_out;

  not not_1 (not_1_out, a);
  not not_2 (not_2_out, b);
  nand nand_1 (nand_1_out, not_1_out, b);
  nand nand_2 (nand_2_out, a, not_2_out);
  nand nand_3 (o, nand_1_out, nand_2_out);
endmodule

module CPU_SHR (
  input  [7:0] i,
  input  shift_in,
  output shift_out,
  output [7:0] o
);

  wire [7:1] cpu_register_8_1__0;

  CPU_REGISTER_8 cpu_register_8_1 (.i(i), .s(1'b1), .e(1'b1), ._0({cpu_register_8_1__0, shift_out}));
  CPU_REGISTER_8 cpu_register_8_2 (.i({shift_in, cpu_register_8_1__0}), .s(1'b1), .e(1'b1), ._0(o));
endmodule

module CPU_SHL (
  input  shift_in,
  input  [7:0] i,
  output [7:0] o,
  output shift_out
);

  wire [6:0] cpu_register_8_1__0;

  CPU_REGISTER_8 cpu_register_8_1 (.i(i), .s(1'b1), .e(1'b1), ._0({shift_out, cpu_register_8_1__0}));
  CPU_REGISTER_8 cpu_register_8_2 (.i({cpu_register_8_1__0, shift_in}), .s(1'b1), .e(1'b1), ._0(o));
endmodule

module CPU_ADDER (
  input  a,
  input  b,
  input  carry_in,
  output sum,
  output carry_out
);

  wire and_1_out, and_2_out, cpu_xor_1_1_o;

  CPU_XOR_1 cpu_xor_1_1 (.a(a), .b(b), .o(cpu_xor_1_1_o));
  and and_1 (and_1_out, carry_in, cpu_xor_1_1_o);
  and and_2 (and_2_out, a, b);
  CPU_XOR_1 cpu_xor_1_2 (.a(cpu_xor_1_1_o), .b(carry_in), .o(sum));
  or or_1 (carry_out, and_1_out, and_2_out);
endmodule

module CPU_ADDER_8 (
  input  [7:0] a,
  input  [7:0] b,
  input  carry_in,
  output carry_out,
  output [7:0] out_5
);

  wire cpu_adder_2_carry_out, cpu_adder_3_carry_out, cpu_adder_4_carry_out, cpu_adder_5_carry_out,
       cpu_adder_6_carry_out, cpu_adder_7_carry_out, cpu_adder_8_carry_out;

  CPU_ADDER cpu_adder_1 (.a(a[0]), .b(b[0]), .carry_in(cpu_adder_2_carry_out), .sum(out_5[0]), .carry_out(carry_out));
  CPU_ADDER cpu_adder_2 (
    .a(a[1]), .b(b[1]), .carry_in(cpu_adder_3_carry_out), .sum(out_5[1]), .carry_out(cpu_adder_2_carry_out));
  CPU_ADDER cpu_adder_3 (
    .a(a[2]), .b(b[2]), .carry_in(cpu_adder_4_carry_out), .sum(out_5[2]), .carry_out(cpu_adder_3_carry_out));
  CPU_ADDER cpu_adder_4 (
    .a(a[3]), .b(b[3]), .carry_in(cpu_adder_5_carry_out), .sum(out_5[3]), .carry_out(cpu_adder_4_carry_out));
  CPU_ADDER cpu_adder_5 (
    .a(a[4]), .b(b[4]), .carry_in(cpu_adder_6_carry_out), .sum(out_5[4]), .carry_out(cpu_adder_5_carry_out));
  CPU_ADDER cpu_adder_6 (
    .a(a[5]), .b(b[5]), .carry_in(cpu_adder_7_carry_out), .sum(out_5[5]), .carry_out(cpu_adder_6_carry_out));
  CPU_ADDER cpu_adder_7 (
    .a(a[6]), .b(b[6]), .carry_in(cpu_adder_8_carry_out), .sum(out_5[6]), .carry_out(cpu_adder_7_carry_out));
  CPU_ADDER cpu_adder_8 (.a(a[7]), .b(b[7]), .carry_in(carry_in), .sum(out_5[7]), .carry_out(cpu_adder_8_carry_out));
endmodule

module CPU_XOR_LE_1 (
  input  above_equal,
  input  a_larger,
  input  a,
  input  b,
  output c,
  output equal,
  output a_large
);

  wire and_2_out, not_1_out;

  CPU_XOR_1 cpu_xor_1_1 (.a(a), .b(b), .o(c));
  not not_1 (not_1_out, c);
  and and_1 (equal, not_1_out, above_equal);
  and and_2 (and_2_out, above_equal, a, c);
  or or_1 (a_large, and_2_out, a_larger);
endmodule

module CPU_XOR_LE_8 (
  input  [7:0] a,
  input  [7:0] b,
  output [7:0] out_3,
  output larger,
  output equal
);

  wire cpu_xor_le_1_1_a_large, cpu_xor_le_1_1_equal, cpu_xor_le_1_2_a_large, cpu_xor_le_1_2_equal,
       cpu_xor_le_1_3_a_large, cpu_xor_le_1_3_equal, cpu_xor_le_1_4_a_large, cpu_xor_le_1_4_equal,
       cpu_xor_le_1_5_a_large, cpu_xor_le_1_5_equal, cpu_xor_le_1_6_a_large, cpu_xor_le_1_6_equal,
       cpu_xor_le_1_7_a_large, cpu_xor_le_1_7_equal;

  CPU_XOR_LE_1 cpu_xor_le_1_1 (
    .a(a[7]), .b(b[7]), .a_larger(1'b0), .c(out_3[0]), .above_equal(1'b1), .equal(cpu_xor_le_1_1_equal),
    .a_large(cpu_xor_le_1_1_a_large));
  CPU_XOR_LE_1 cpu_xor_le_1_2 (
    .a(a[6]), .b(b[6]), .a_larger(cpu_xor_le_1_1_a_large), .c(out_3[1]), .above_equal(cpu_xor_le_1_1_equal),
    .equal(cpu_xor_le_1_2_equal), .a_large(cpu_xor_le_1_2_a_large));
  CPU_XOR_LE_1 cpu_xor_le_1_3 (
    .a(a[5]), .b(b[5]), .a_larger(cpu_xor_le_1_2_a_large), .c(out_3[2]), .above_equal(cpu_xor_le_1_2_equal),
    .equal(cpu_xor_le_1_3_equal), .a_large(cpu_xor_le_1_3_a_large));
  CPU_XOR_LE_1 cpu_xor_le_1_4 (
    .a(a[4]), .b(b[4]), .a_larger(cpu_xor_le_1_3_a_large), .c(out_3[3]), .above_equal(cpu_xor_le_1_3_equal),
    .equal(cpu_xor_le_1_4_equal), .a_large(cpu_xor_le_1_4_a_large));
  CPU_XOR_LE_1 cpu_xor_le_1_5 (
    .a(a[3]), .b(b[3]), .a_larger(cpu_xor_le_1_4_a_large), .c(out_3[4]), .above_equal(cpu_xor_le_1_4_equal),
    .equal(cpu_xor_le_1_5_equal), .a_large(cpu_xor_le_1_5_a_large));
  CPU_XOR_LE_1 cpu_xor_le_1_6 (
    .a(a[2]), .b(b[2]), .a_larger(cpu_xor_le_1_5_a_large), .c(out_3[5]), .above_equal(cpu_xor_le_1_5_equal),
    .equal(cpu_xor_le_1_6_equal), .a_large(cpu_xor_le_1_6_a_large));
  CPU_XOR_LE_1 cpu_xor_le_1_7 (
    .a(a[1]), .b(b[1]), .a_larger(cpu_xor_le_1_6_a_large), .c(out_3[6]), .above_equal(cpu_xor_le_1_6_equal),
    .equal(cpu_xor_le_1_7_equal), .a_large(cpu_xor_le_1_7_a_large));
  CPU_XOR_LE_1 cpu_xor_le_1_8 (
    .a(a[0]), .b(b[0]), .a_larger(cpu_xor_le_1_7_a_large), .c(out_3[7]), .above_equal(cpu_xor_le_1_7_equal),
    .equal(equal), .a_large(larger));
endmodule

module CPU_Z (
  input  [7:0] i,
  output o
);

  wire or_1_out;

  or or_1 (or_1_out, i[0], i[1], i[2], i[3], i[4], i[5], i[6], i[7]);
  not not_1 (o, or_1_out);
endmodule

module CPU_DECODER_3x8 (
  input  a,
  input  b,
  input  c,
  output [7:0] o
);

  wire not_1_out, not_2_out, not_3_out;

  not not_1 (not_1_out, c);
  not not_2 (not_2_out, b);
  not not_3 (not_3_out, a);
  and and_1 (o[0], not_3_out, not_2_out, not_1_out);
  and and_2 (o[1], not_3_out, not_2_out, c);
  and and_3 (o[2], not_3_out, b, not_1_out);
  and and_4 (o[3], not_3_out, b, c);
  and and_5 (o[4], a, not_2_out, not_1_out);
  and and_6 (o[5], a, not_2_out, c);
  and and_7 (o[6], a, b, not_1_out);
  and and_8 (o[7], a, b, c);

  // Notes on the sheet:
  //   c: pull=down
  //   b: pull=down
  //   o: pull=down
  //   a: pull=down
endmodule

module CPU_E (
  input  [7:0] in_1,
  input  in_2,
  output [7:0] out_3
);

  wire and_1_out, and_2_out, and_3_out, and_4_out, and_5_out, and_6_out, and_7_out, and_8_out;

  and and_1 (and_1_out, in_1[0], in_2);
  assign out_3[0] = in_2 ? and_1_out : 1'bz;  // Controlled_Buffer controlled_buffer_1
  and and_2 (and_2_out, in_1[1], in_2);
  assign out_3[1] = in_2 ? and_2_out : 1'bz;  // Controlled_Buffer controlled_buffer_2
  and and_3 (and_3_out, in_1[2], in_2);
  assign out_3[2] = in_2 ? and_3_out : 1'bz;  // Controlled_Buffer controlled_buffer_3
  and and_4 (and_4_out, in_1[3], in_2);
  assign out_3[3] = in_2 ? and_4_out : 1'bz;  // Controlled_Buffer controlled_buffer_4
  and and_5 (and_5_out, in_1[4], in_2);
  assign out_3[4] = in_2 ? and_5_out : 1'bz;  // Controlled_Buffer controlled_buffer_5
  and and_6 (and_6_out, in_1[5], in_2);
  assign out_3[5] = in_2 ? and_6_out : 1'bz;  // Controlled_Buffer controlled_buffer_6
  and and_7 (and_7_out, in_1[6], in_2);
  assign out_3[6] = in_2 ? and_7_out : 1'bz;  // Controlled_Buffer controlled_buffer_7
  and and_8 (and_8_out, in_1[7], in_2);
  assign out_3[7] = in_2 ? and_8_out : 1'bz;  // Controlled_Buffer controlled_buffer_8
endmodule

module CPU_ALU (
  input  [7:0] a,
  input  [7:0] b,
  input  carry_in,
  input  a_2,
  input  b_2,
  input  c,
  output a_larger,
  output equal,
  output zero,
  output [7:0] c_2,
  output carry_out
);

  wire and_1_out, and_2_out, and_3_out, cpu_adder_8_1_carry_out, cpu_shl_1_shift_out, cpu_shr_1_shift_out;
  wire [7:0] cpu_adder_8_1_out_5, cpu_and_1_o, cpu_decoder_3x8_1_o, cpu_not_1_out_2, cpu_or_1__0,
       cpu_shl_1_o, cpu_shr_1_o, cpu_xor_le_8_1_out_3;

  CPU_XOR_LE_8 cpu_xor_le_8_1 (.a(a), .b(b), .out_3(cpu_xor_le_8_1_out_3), .larger(a_larger), .equal(equal));
  CPU_AND cpu_and_1 (.a(a), .o(cpu_and_1_o), .b(b));
  CPU_NOT cpu_not_1 (.i(a), .out_2(cpu_not_1_out_2));
  CPU_SHL cpu_shl_1 (.shift_in(carry_in), .i(a), .o(cpu_shl_1_o), .shift_out(cpu_shl_1_shift_out));
  CPU_SHR cpu_shr_1 (.shift_out(cpu_shr_1_shift_out), .i(a), .o(cpu_shr_1_o), .shift_in(carry_in));
  CPU_ADDER_8 cpu_adder_8_1 (
    .a(a), .b(b), .carry_out(cpu_adder_8_1_carry_out), .out_5(cpu_adder_8_1_out_5), .carry_in(carry_in));
  CPU_OR cpu_or_1 (.a(a), .b(b), ._0(cpu_or_1__0));
  CPU_DECODER_3x8 cpu_decoder_3x8_1 (.a(a_2), .b(b_2), .c(c), .o(cpu_decoder_3x8_1_o));
  CPU_E cpu_e_1 (.in_1(cpu_xor_le_8_1_out_3), .out_3(c_2), .in_2(cpu_decoder_3x8_1_o[6]));
  CPU_E cpu_e_2 (.in_1(cpu_or_1__0), .out_3(c_2), .in_2(cpu_decoder_3x8_1_o[5]));
  CPU_E cpu_e_3 (.in_1(cpu_and_1_o), .out_3(c_2), .in_2(cpu_decoder_3x8_1_o[4]));
  CPU_E cpu_e_4 (.in_1(cpu_not_1_out_2), .out_3(c_2), .in_2(cpu_decoder_3x8_1_o[3]));
  CPU_E cpu_e_5 (.in_1(cpu_shl_1_o), .out_3(c_2), .in_2(cpu_decoder_3x8_1_o[2]));
  CPU_E cpu_e_6 (.in_1(cpu_shr_1_o), .out_3(c_2), .in_2(cpu_decoder_3x8_1_o[1]));
  CPU_E cpu_e_7 (.in_1(cpu_adder_8_1_out_5), .out_3(c_2), .in_2(cpu_decoder_3x8_1_o[0]));
  and and_1 (and_1_out, cpu_shl_1_shift_out, cpu_decoder_3x8_1_o[2]);
  assign carry_out = cpu_decoder_3x8_1_o[2] ? and_1_out : 1'bz;  // Controlled_Buffer controlled_buffer_1
  and and_2 (and_2_out, cpu_shr_1_shift_out, cpu_decoder_3x8_1_o[1]);
  assign carry_out = cpu_decoder_3x8_1_o[1] ? and_2_out : 1'bz;  // Controlled_Buffer controlled_buffer_2
  and and_3 (and_3_out, cpu_adder_8_1_carry_out, cpu_decoder_3x8_1_o[0]);
  assign carry_out = cpu_decoder_3x8_1_o[0] ? and_3_out : 1'bz;  // Controlled_Buffer controlled_buffer_3
  CPU_Z cpu_z_1 (.i(c_2), .o(zero));

  // Notes on the sheet:
  //   zero: pull=down
  //   equal: pull=down
  //   a: pull=down
  //   carry_out: pull=down
  //   a_larger: pull=down
  //   c: pull=down
  //   b: pull=down
  //   carry_in: pull=down
  //   a_2: pull=down
  //   b_2: pull=down
  //   c_2: pull=down
endmodule

module CPU_BUS_1 (
  input  [7:0] i,
  input  bus_1,
  output [7:0] o
);

  wire not_1_out;

  and and_1 (o[7], i[7], not_1_out);
  and and_2 (o[6], i[6], not_1_out);
  and and_3 (o[5], i[5], not_1_out);
  and and_4 (o[3], i[3], not_1_out);
  and and_5 (o[4], i[4], not_1_out);
  and and_6 (o[2], i[2], not_1_out);
  and and_7 (o[1], i[1], not_1_out);
  not not_1 (not_1_out, bus_1);
  or or_1 (o[0], i[0], bus_1);

  // Notes on the sheet:
  //   i: pull=down
  //   o: pull=down
  //   bus_1: pull=down
endmodule

module CPU_ACCUMULATOR (
  input  [7:0] i,
  input  s,
  input  e,
  output [7:0] o
);

  CPU_REGISTER_8 cpu_register_8_1 (.i(i), .s(s), .e(e), ._0(o));

  // Notes on the sheet:
  //   s: pull=down
  //   i: pull=down
  //   e: pull=down
  //   o: pull=down
endmodule

module CPU_R (
  input  [7:0] i,
  input  s,
  input  e,
  output [7:0] o
);

  CPU_REGISTER_8 cpu_register_8_1 (.i(i), .s(s), .e(e), ._0(o));

  // Notes on the sheet:
  //   i: pull=down
  //   o: pull=down
  //   s: pull=down
  //   e: pull=down
endmodule

module CPU_TMP (
  input  [7:0] i,
  input  s,
  output [7:0] o
);

  wire [7:0] controlled_buffer_1_out;

  assign controlled_buffer_1_out = s ? i : 8'bz;  // Controlled_Buffer controlled_buffer_1
  CPU_MEM_8 cpu_mem_8_1 (.s(s), .in_1(controlled_buffer_1_out), .out_3(o));

  // Notes on the sheet:
  //   o: pull=down
  //   s: pull=down
  //   i: pull=down
endmodule

module CPU_STEPPER (
  input  reset,
  input  clk,
  output step_1,
  output step_2,
  output step_3,
  output step_4,
  output step_5,
  output step_6,
  output step_7
);

  wire cpu_mem_1_1_out_3, cpu_mem_1_2_out_3, cpu_mem_1_3_out_3, cpu_mem_1_4_out_3, cpu_mem_1_5_out_3,
       cpu_mem_1_6_out_3, cpu_mem_1_7_out_3, cpu_mem_1_8_out_3, cpu_mem_1_9_out_3, cpu_mem_1_10_out_3,
       cpu_mem_1_11_out_3, not_1_out, not_2_out, not_3_out, not_4_out, not_5_out, not_6_out, not_7_out,
       not_8_out, or_1_out, or_2_out;

  not not_1 (not_1_out, clk);
  not not_2 (not_2_out, reset);
  or or_1 (or_1_out, reset, clk);
  or or_2 (or_2_out, reset, not_1_out);
  or or_3 (step_1, reset, not_3_out);
  CPU_MEM_1 cpu_mem_1_1 (.in_1(not_2_out), .in_2(or_1_out), .out_3(cpu_mem_1_1_out_3));
  not not_3 (not_3_out, cpu_mem_1_2_out_3);
  CPU_MEM_1 cpu_mem_1_2 (.in_1(cpu_mem_1_1_out_3), .in_2(or_2_out), .out_3(cpu_mem_1_2_out_3));
  and and_1 (step_2, cpu_mem_1_2_out_3, not_4_out);
  not not_4 (not_4_out, cpu_mem_1_4_out_3);
  CPU_MEM_1 cpu_mem_1_3 (.in_1(cpu_mem_1_2_out_3), .in_2(or_1_out), .out_3(cpu_mem_1_3_out_3));
  CPU_MEM_1 cpu_mem_1_4 (.in_1(cpu_mem_1_3_out_3), .in_2(or_2_out), .out_3(cpu_mem_1_4_out_3));
  and and_2 (step_3, cpu_mem_1_4_out_3, not_5_out);
  CPU_MEM_1 cpu_mem_1_5 (.in_1(cpu_mem_1_4_out_3), .in_2(or_1_out), .out_3(cpu_mem_1_5_out_3));
  not not_5 (not_5_out, cpu_mem_1_6_out_3);
  CPU_MEM_1 cpu_mem_1_6 (.in_1(cpu_mem_1_5_out_3), .in_2(or_2_out), .out_3(cpu_mem_1_6_out_3));
  and and_3 (step_4, cpu_mem_1_6_out_3, not_6_out);
  not not_6 (not_6_out, cpu_mem_1_8_out_3);
  CPU_MEM_1 cpu_mem_1_7 (.in_1(cpu_mem_1_6_out_3), .in_2(or_1_out), .out_3(cpu_mem_1_7_out_3));
  and and_4 (step_5, cpu_mem_1_8_out_3, not_7_out);
  CPU_MEM_1 cpu_mem_1_8 (.in_1(cpu_mem_1_7_out_3), .in_2(or_2_out), .out_3(cpu_mem_1_8_out_3));
  CPU_MEM_1 cpu_mem_1_9 (.in_1(cpu_mem_1_8_out_3), .in_2(or_1_out), .out_3(cpu_mem_1_9_out_3));
  not not_7 (not_7_out, cpu_mem_1_10_out_3);
  CPU_MEM_1 cpu_mem_1_10 (.in_1(cpu_mem_1_9_out_3), .in_2(or_2_out), .out_3(cpu_mem_1_10_out_3));
  and and_5 (step_6, cpu_mem_1_10_out_3, not_8_out);
  CPU_MEM_1 cpu_mem_1_11 (.in_1(cpu_mem_1_10_out_3), .in_2(or_1_out), .out_3(cpu_mem_1_11_out_3));
  not not_8 (not_8_out, step_7);
  CPU_MEM_1 cpu_mem_1_12 (.in_1(cpu_mem_1_11_out_3), .in_2(or_2_out), .out_3(step_7));

  // Notes on the sheet:
  //   reset: pull=down
endmodule

module CPU (
  input  [7:0] s,
  input  [7:0] s_2,
  input  [7:0] in_3
);

  wire clock_1_out, cpu_clk_1_clk, cpu_clk_1_clke, cpu_clk_1_clks, cpu_control_section_1_acc_e,
       cpu_control_section_1_acc_s, cpu_control_section_1_alu_0, cpu_control_section_1_alu_1,
       cpu_control_section_1_alu_2, cpu_control_section_1_bus_1, cpu_control_section_1_iar_e,
       cpu_control_section_1_iar_s, cpu_control_section_1_mar_s, cpu_control_section_1_r0_e,
       cpu_control_section_1_r0_s, cpu_control_section_1_r1_e, cpu_control_section_1_r2_e,
       cpu_control_section_1_r2_s, cpu_control_section_1_r3_e, cpu_control_section_1_ram_e,
       cpu_control_section_1_ram_s, cpu_control_section_1_tmp_s;
  wire [7:0] cpu_accumulator_1_o, cpu_alu_1_c_2, cpu_bus_1_1_o, cpu_ir_1_o, cpu_tmp_1_o;

  CPU_ACCUMULATOR cpu_accumulator_1 (
    .i(cpu_alu_1_c_2), .o(cpu_accumulator_1_o), .s(cpu_control_section_1_acc_s),
    .e(cpu_control_section_1_acc_e));
  CPU_TMP cpu_tmp_1 (.i(cpu_accumulator_1_o), .o(cpu_tmp_1_o), .s(cpu_control_section_1_tmp_s));
  CPU_BUS_1 cpu_bus_1_1 (.i(cpu_tmp_1_o), .bus_1(cpu_control_section_1_bus_1), .o(cpu_bus_1_1_o));
  CPU_ALU cpu_alu_1 (
    .a(cpu_accumulator_1_o), .b(cpu_bus_1_1_o), .carry_in(1'b0), .a_2(cpu_control_section_1_alu_0),
    .b_2(cpu_control_section_1_alu_1), .c(cpu_control_section_1_alu_2), .c_2(cpu_alu_1_c_2));  // open: zero, carry_out, a_larger, equal
  Clock clock_1 (.out(clock_1_out));
  CPU_CLK cpu_clk_1 (.clkin(clock_1_out), .clks(cpu_clk_1_clks), .clke(cpu_clk_1_clke), .clk(cpu_clk_1_clk));
  CPU_CONTROL_SECTION cpu_control_section_1 (
    .clks(cpu_clk_1_clks), .clke(cpu_clk_1_clke), .clk(cpu_clk_1_clk), .MAR_S(cpu_control_section_1_mar_s),
    .ACC_S(cpu_control_section_1_acc_s), .TMP_S(cpu_control_section_1_tmp_s),
    .RAM_S(cpu_control_section_1_ram_s), .IAR_E(cpu_control_section_1_iar_e),
    .RAM_E(cpu_control_section_1_ram_e), .BUS_1(cpu_control_section_1_bus_1),
    .ACC_E(cpu_control_section_1_acc_e), .IAR_S(cpu_control_section_1_iar_s),
    .R0_S(cpu_control_section_1_r0_s), .R2_S(cpu_control_section_1_r2_s), .R0_E(cpu_control_section_1_r0_e),
    .R1_E(cpu_control_section_1_r1_e), .R2_E(cpu_control_section_1_r2_e), .R3_E(cpu_control_section_1_r3_e),
    .IR_IN(cpu_ir_1_o), .ALU_0(cpu_control_section_1_alu_0), .ALU_1(cpu_control_section_1_alu_1),
    .ALU_2(cpu_control_section_1_alu_2));  // open: FLAGS_S, IO_CLKS_S, IO_CLK_E, IR_S, R1_S, R3_S
  CPU_R cpu_r_1 (
    .i(cpu_accumulator_1_o), .o(cpu_accumulator_1_o), .s(cpu_control_section_1_r0_s),
    .e(cpu_control_section_1_r0_e));
  CPU_IAR cpu_iar_1 (
    .i(cpu_accumulator_1_o), .o(cpu_accumulator_1_o), .s(cpu_control_section_1_iar_s),
    .e(cpu_control_section_1_iar_e));
  CPU_R cpu_r_2 (.i(cpu_accumulator_1_o), .o(cpu_accumulator_1_o), .s(1'b1), .e(cpu_control_section_1_r1_e));
  CPU_R cpu_r_3 (.i(s), .o(cpu_accumulator_1_o), .s(1'b1), .e(cpu_control_section_1_r2_e));
  CPU_IR cpu_ir_1 (.i(in_3), .o(cpu_ir_1_o), .s(1'b1));
  CPU_R cpu_r_4 (.i(s_2), .o(cpu_accumulator_1_o), .s(1'b1), .e(cpu_control_section_1_r3_e));
  CPU_RAM_256 cpu_ram_256_1 (
    .o(cpu_accumulator_1_o), .sa(cpu_control_section_1_mar_s), .address(cpu_accumulator_1_o),
    .s(cpu_control_section_1_ram_s), .e(cpu_control_section_1_ram_e), .i(cpu_accumulator_1_o));
endmodule

module CPU_IAR (
  input  [7:0] i,
  input  s,
  input  e,
  output [7:0] o
);

  CPU_REGISTER_8 cpu_register_8_1 (.i(i), .s(s), .e(e), ._0(o));

  // Notes on the sheet:
  //   o: pull=down
  //   s: pull=down
  //   i: pull=down
  //   e: pull=down
endmodule

module CPU_IR (
  input  [7:0] i,
  input  s,
  output [7:0] o
);

  CPU_REGISTER_8 cpu_register_8_1 (.i(i), .s(s), .e(s), ._0(o));

  // Notes on the sheet:
  //   s: pull=down
  //   i: pull=down
  //   o: pull=down
endmodule

module CPU_FLAGS (
  input  C,
  input  A,
  input  E,
  input  Z,
  input  s,
  output C_2,
  output A_2,
  output E_2,
  output Z_2
);

  CPU_MEM_1 cpu_mem_1_1 (.in_1(C), .in_2(s), .out_3(C_2));
  CPU_MEM_1 cpu_mem_1_2 (.in_1(A), .in_2(s), .out_3(A_2));
  CPU_MEM_1 cpu_mem_1_3 (.in_1(E), .in_2(s), .out_3(E_2));
  CPU_MEM_1 cpu_mem_1_4 (.in_1(Z), .in_2(s), .out_3(Z_2));

  // Notes on the sheet:
  //   A: pull=down
  //   A_2: pull=down
  //   Z: pull=down
  //   C_2: pull=down
  //   E: pull=down
  //   Z_2: pull=down
  //   C: pull=down
  //   E_2: pull=down
endmodule

module CPU_CONTROL_SECTION (
  input  clks,
  input  clk,
  input  clke,
  input  [7:0] IR_IN,
  output BUS_1,
  output IR_S,
  output MAR_S,
  output IAR_E,
  output RAM_E,
  output IAR_S,
  output ACC_E,
  output ACC_S,
  output IO_CLK_E,
  output RAM_S,
  output TMP_S,
  output FLAGS_S,
  output IO_CLKS_S,
  output R0_S,
  output R0_E,
  output R1_S,
  output R1_E,
  output R2_E,
  output R2_S,
  output R3_E,
  output R3_S,
  output ALU_0,
  output ALU_1,
  output ALU_2
);

  wire and_5_out, and_6_out, and_7_out, and_8_out, and_10_out, and_11_out, and_12_out, and_13_out,
       and_14_out, and_21_out, and_22_out, cpu_decoder_2x4_1__0, cpu_decoder_2x4_1__1, cpu_decoder_2x4_1__2,
       cpu_decoder_2x4_1__3, cpu_decoder_2x4_west_1__0, cpu_decoder_2x4_west_1__1, cpu_decoder_2x4_west_1__2,
       cpu_decoder_2x4_west_1__3, cpu_decoder_2x4_west_2__0, cpu_decoder_2x4_west_2__1,
       cpu_decoder_2x4_west_2__2, cpu_decoder_2x4_west_2__3, cpu_decoder_cntrl_3x8_1__0,
       cpu_decoder_cntrl_3x8_1__1, cpu_decoder_cntrl_3x8_1__2, cpu_decoder_cntrl_3x8_1__3,
       cpu_decoder_cntrl_3x8_1__4, cpu_decoder_cntrl_3x8_1__5, cpu_decoder_cntrl_3x8_1__6,
       cpu_decoder_cntrl_3x8_1__7, cpu_stepper_1_step_4, cpu_stepper_1_step_5, cpu_stepper_1_step_7, MAR_S_t,
       not_1_out, RAM_E_t, RAM_S_t;

  buf or_1 (R0_E, and_5_out);  // OR_Gate
  or or_2 (R1_E, and_6_out, and_10_out);
  or or_3 (R2_E, and_7_out, and_11_out);
  or or_4 (R3_E, and_8_out, and_12_out);
  and and_1 (IAR_E, clke, 1'b0);
  and and_2 (RAM_E, clke, RAM_E_t);
  and and_3 (ACC_E, clke, 1'b0);
  and and_4 (IO_CLK_E, clke, 1'b0);
  and and_5 (and_5_out, clke, RAM_S_t, cpu_decoder_2x4_west_1__0);
  and and_6 (and_6_out, clke, RAM_S_t, cpu_decoder_2x4_west_1__1);
  and and_7 (and_7_out, clke, RAM_S_t, cpu_decoder_2x4_west_1__2);
  and and_8 (and_8_out, clke, RAM_S_t, cpu_decoder_2x4_west_1__3);
  and and_9 (and_5_out, clke, MAR_S_t, cpu_decoder_2x4_west_2__0);
  and and_10 (and_10_out, clke, MAR_S_t, cpu_decoder_2x4_west_2__1);
  and and_11 (and_11_out, clke, MAR_S_t, cpu_decoder_2x4_west_2__2);
  and and_12 (and_12_out, clke, MAR_S_t, cpu_decoder_2x4_west_2__3);
  CPU_DECODER_2x4_WEST cpu_decoder_2x4_west_1 (
    .a(IR_IN[0]), .b(IR_IN[1]), ._0(cpu_decoder_2x4_west_1__0), ._1(cpu_decoder_2x4_west_1__1),
    ._2(cpu_decoder_2x4_west_1__2), ._3(cpu_decoder_2x4_west_1__3));
  CPU_DECODER_2x4_WEST cpu_decoder_2x4_west_2 (
    .a(IR_IN[2]), .b(IR_IN[3]), ._0(cpu_decoder_2x4_west_2__0), ._1(cpu_decoder_2x4_west_2__1),
    ._2(cpu_decoder_2x4_west_2__2), ._3(cpu_decoder_2x4_west_2__3));
  CPU_STEPPER cpu_stepper_1 (
    .step_1(BUS_1), .step_4(cpu_stepper_1_step_4), .step_5(cpu_stepper_1_step_5),
    .step_7(cpu_stepper_1_step_7), .reset(cpu_stepper_1_step_7), .clk(clk));  // open: step_2, step_3, step_6
  not not_1 (not_1_out, IR_IN[7]);
  CPU_DECODER_CNTRL_3x8 cpu_decoder_cntrl_3x8_1 (
    .a(IR_IN[6]), .b(IR_IN[5]), .c(IR_IN[4]), ._0(cpu_decoder_cntrl_3x8_1__0),
    ._1(cpu_decoder_cntrl_3x8_1__1), ._2(cpu_decoder_cntrl_3x8_1__2), ._3(cpu_decoder_cntrl_3x8_1__3),
    ._4(cpu_decoder_cntrl_3x8_1__4), ._5(cpu_decoder_cntrl_3x8_1__5), ._6(cpu_decoder_cntrl_3x8_1__6),
    ._7(cpu_decoder_cntrl_3x8_1__7));
  and and_13 (and_13_out, not_1_out, cpu_decoder_cntrl_3x8_1__0);
  and and_14 (and_14_out, not_1_out, cpu_decoder_cntrl_3x8_1__1);
  // AND_Gate and_15 has open pins: in0=not_1_out, in1=cpu_decoder_cntrl_3x8_1__2, out=open
  // AND_Gate and_16 has open pins: in0=not_1_out, in1=cpu_decoder_cntrl_3x8_1__3, out=open
  // AND_Gate and_17 has open pins: in0=not_1_out, in1=cpu_decoder_cntrl_3x8_1__4, out=open
  // AND_Gate and_18 has open pins: in0=not_1_out, in1=cpu_decoder_cntrl_3x8_1__5, out=open
  // AND_Gate and_19 has open pins: in0=not_1_out, in1=cpu_decoder_cntrl_3x8_1__6, out=open
  // AND_Gate and_20 has open pins: in0=not_1_out, in1=cpu_decoder_cntrl_3x8_1__7, out=open
  or or_5 (MAR_S_t, and_21_out, and_22_out);
  and and_21 (and_21_out, cpu_stepper_1_step_4, and_13_out);
  and and_22 (and_22_out, cpu_stepper_1_step_4, and_14_out);
  and and_23 (RAM_E_t, cpu_stepper_1_step_5, and_13_out);
  and and_24 (RAM_S_t, cpu_stepper_1_step_5, and_14_out);
  CPU_DECODER_2x4 cpu_decoder_2x4_1 (
    .a(IR_IN[0]), .b(IR_IN[1]), ._0(cpu_decoder_2x4_1__0), ._1(cpu_decoder_2x4_1__1),
    ._2(cpu_decoder_2x4_1__2), ._3(cpu_decoder_2x4_1__3));
  and and_25 (IR_S, clks, 1'b0);
  and and_26 (MAR_S, clks, MAR_S_t);
  and and_27 (IAR_S, clks, 1'b0);
  and and_28 (ACC_S, clks, 1'b0);
  and and_29 (RAM_S, clks, RAM_S_t);
  and and_30 (TMP_S, clks, 1'b0);
  and and_31 (FLAGS_S, clks, 1'b0);
  and and_32 (IO_CLKS_S, clks, 1'b0);
  and and_33 (R0_S, clks, RAM_E_t, cpu_decoder_2x4_1__0);
  and and_34 (R1_S, clks, RAM_E_t, cpu_decoder_2x4_1__1);
  and and_35 (R2_S, clks, RAM_E_t, cpu_decoder_2x4_1__2);
  and and_36 (R3_S, clks, RAM_E_t, cpu_decoder_2x4_1__3);

  // Other names for the same wires on the sheet: REGA_E = MAR_S_t; REGB_E = RAM_S_t; REGB_S = RAM_E_t

  // Notes on the sheet:
  //   REG B_E
  //   REG A
  //   ENABLE ONTO BUS
  //   REG B
  //   REG A
  //   SET INTO REGISTER
  //   REG B_S
endmodule

module CPU_CLK (
  input  clkin,
  output clk,
  output clks,
  output clke
);

  wire j_k_ff_1_qn, nand_1_out;

  J_K_Flip_Flop j_k_ff_1 (.J(1'b1), .clk(clkin), .K(1'b1), .Q(clk), .Qn(j_k_ff_1_qn));  // open: preset, en, reset
  nand nand_1 (nand_1_out, clkin, clk);
  nand nand_2 (clke, j_k_ff_1_qn, clkin);
  not not_1 (clks, nand_1_out);

  // Notes on the sheet:
  //   clk: pull=down
  //   clke: pull=down
  //   clks: pull=down
  //   clkin: pull=down
endmodule

module CPU_DECODER_2x4 (
  input  a,
  input  b,
  output _0,
  output _1,
  output _2,
  output _3
);

  wire not_1_out, not_2_out;

  not not_1 (not_1_out, b);
  not not_2 (not_2_out, a);
  and and_1 (_0, not_2_out, not_1_out);
  and and_2 (_1, a, not_1_out);
  and and_3 (_2, b, not_2_out);
  and and_4 (_3, b, a);

  // Notes on the sheet:
  //   a: pull=down
  //   b: pull=down
endmodule

module CPU_DECODER_2x4_WEST (
  input  a,
  input  b,
  output _0,
  output _1,
  output _2,
  output _3
);

  wire not_1_out, not_2_out;

  not not_1 (not_1_out, b);
  not not_2 (not_2_out, a);
  and and_1 (_0, not_2_out, not_1_out);
  and and_2 (_1, a, not_1_out);
  and and_3 (_2, b, not_2_out);
  and and_4 (_3, b, a);

  // Notes on the sheet:
  //   a: pull=down
  //   b: pull=down
endmodule

module CPU_DECODER_CNTRL_3x8 (
  input  a,
  input  b,
  input  c,
  output _0,
  output _1,
  output _2,
  output _3,
  output _4,
  output _5,
  output _6,
  output _7
);

  wire not_1_out, not_2_out, not_3_out;

  not not_1 (not_1_out, c);
  not not_2 (not_2_out, b);
  not not_3 (not_3_out, a);
  and and_1 (_0, not_3_out, not_2_out, not_1_out);
  and and_2 (_1, not_3_out, not_2_out, c);
  and and_3 (_2, not_3_out, b, not_1_out);
  and and_4 (_3, not_3_out, b, c);
  and and_5 (_4, a, not_2_out, not_1_out);
  and and_6 (_5, a, not_2_out, c);
  and and_7 (_6, a, b, not_1_out);
  and and_8 (_7, a, b, c);

  // Notes on the sheet:
  //   c: pull=down
  //   a: pull=down
  //   b: pull=down
endmodule
