// Logisim project jk-flip-flop.circ as structural Verilog: 1 circuit, main circuit main
module main (
  input  in_1,
  input  in_2,
  input  in_3,
  input  in_4
);

  wire clock_1_out, j_k_ff_1_q, j_k_ff_1_qn, nand_1_out, nand_2_out, nor_1_out, nor_2_out;

  Clock clock_1 (.out(clock_1_out));
  nand nand_1 (nand_1_out, nor_1_out, in_1, clock_1_out);
  nand nand_2 (nand_2_out, clock_1_out, in_2, nor_2_out);
  nor nor_1 (nor_1_out, nand_1_out, nor_2_out);
  nor nor_2 (nor_2_out, nor_1_out, nand_2_out);
  J_K_Flip_Flop j_k_ff_1 (.J(in_3), .K(in_4), .Q(j_k_ff_1_q), .Qn(j_k_ff_1_qn));  // open: clk, preset, en, reset
  LED led_1 (.in(j_k_ff_1_q));
  LED led_2 (.in(j_k_ff_1_qn));
  LED led_3 (.in(nor_1_out));
  LED led_4 (.in(nor_2_out));
endmodule
