// Logisim project sr-flip-flop.circ as structural Verilog: 2 circuits, main circuit main
module main (
  input  in_1,
  input  in_2,
  input  in_3,
  input  in_4,
  input  in_5,
  input  in_6,
  input  s,
  input  r,
  output out_9
);

  wire clock_1_out, nand_1_out, nand_2_out, nand_3_out, nand_4_out, nor_1_out, nor_2_out, s_r_ff_1_q,
       s_r_ff_1_qn;

  Clock clock_1 (.out(clock_1_out));
  nand nand_1 (nand_1_out, in_1, in_1, clock_1_out);
  nand nand_2 (nand_2_out, clock_1_out, in_2);
  LED led_1 (.in(s_r_ff_1_q));
  S_R_Flip_Flop s_r_ff_1 (.S(in_5), .R(in_6), .Q(s_r_ff_1_q), .Qn(s_r_ff_1_qn));  // open: clk, preset, reset, en
  LED led_2 (.in(s_r_ff_1_qn));
  nor nor_1 (nor_1_out, nand_1_out, nor_2_out);
  nor nor_2 (nor_2_out, nor_1_out, nand_2_out);
  nand nand_3 (nand_3_out, s, nand_4_out);
  nand nand_4 (nand_4_out, nand_3_out, r);
  LED led_3 (.in(nor_1_out));
  LED led_4 (.in(nor_2_out));
  LED led_5 (.in(nand_3_out));
  LED led_6 (.in(nand_4_out));
  CPU_MEM_1 cpu_mem_1_1 (.s(in_3), .e(in_4), .e_2(out_9));

  // Notes on the sheet:
  //   q
  //   nq
endmodule

module CPU_MEM_1 (
  input  s,
  input  e,
  output e_2
);

  wire nand_1_out, nand_2_out, nand_4_out;

  nand nand_1 (nand_1_out, s, e);
  nand nand_2 (nand_2_out, nand_1_out, e);
  nand nand_3 (e_2, nand_1_out, nand_4_out);
  nand nand_4 (nand_4_out, e_2, nand_2_out);
endmodule
